// Logisim project sqrt2.circ as structural Verilog: 35 circuits, main circuit main
module main (
  input  ENABLE,
  input  [15:0] IO_DATA_IN,
  output NAN,
  output PINF,
  output NINF,
  output RESULT,
  output [15:0] IO_DATA_OUT
);

  wire CLK_out;

  Clock CLK (.out(CLK_out));
  sqrt sqrt_1 (
    .CLK(CLK_out), .ENABLE(ENABLE), .IO_DATA_IN(IO_DATA_IN), .IS_NAN(NAN), .IS_PINF(PINF), .IS_NINF(NINF),
    .RESULT(RESULT), .IO_DATA_OUT(IO_DATA_OUT));
endmodule

module sqrt (
  input  CLK,
  input  ENABLE,
  input  [15:0] IO_DATA_IN,
  output IS_NAN,
  output IS_PINF,
  output IS_NINF,
  output RESULT,
  output [15:0] IO_DATA_OUT
);

  wire and_1_out, and_2_out, and_3_out, and_4_out, and_5_out, and_8_out, and_9_out,
       comporator_3byte_1_num1_greater, comporator_3byte_2_num1_greater, comporator_3byte_3_num1_greater,
       comporator_3byte_4_equal, comporator_3byte_4_num1_greater, is_12_tact, is_first_tact, is_NaN_t,
       is_neg_zero_1_result, is_pos_inf_1_result, is_pos_zero_1_result, is_qNaN, is_spec_case, is_zero_tact,
       not_1_out, not_3_out, not_4_out, not_5_out, not_6_out, not_7_out, not_8_out, not_9_out, not_10_out,
       not_11_out, not_12_out, or_1_out, or_2_out, or_3_out, or_4_out, or_5_out, rsc_trigger_1_not_q,
       rsc_trigger_1_q, rsc_trigger_2_not_q, rsc_trigger_2_q, rsc_trigger_3_not_q, rsc_trigger_3_q,
       rsc_trigger_4_not_q;
  wire [3:0] COUNTER_TACT_value_4bit;
  wire [4:0] parsing_1_exp_5bit;
  wire [9:0] mant_res, parsing_1_mant_10bit;
  wire [15:0] calmed_down_nan_1_result, if_16bit_2_result, if_16bit_3_result, not_2_out, quite_nan_1_qnan,
       spec_case, transistor_1_out, transmission_1_p1;
  wire [15:15] parsing_1_sign;
  wire [23:0] bit_extender_1_out, bit_extender_2_out, bit_extender_3_out, exp_write_out_num,
       if_0_than_exp_0_result, if_24bit_1_result, if_24bit_2_result, if_24bit_3_result,
       install_data_1_res_exp, install_data_1_res_mant, left_shift_1_res_24bit, left_shift_2_res_24bit,
       left_shift_3_res_24bit, left_shift_4_res_24bit, left_shift_5_res_24bit, left_shift_6_res_24bit,
       NUM_READ_out_num, NUM_WRITE_out_num, remainder_read_out_num, remainder_write_out_num, res_exp,
       res_write_out_num, spec_case_read_out_num, spec_case_write_out_num, substractor_3byte_1_res_24bit,
       summator_3byte_1_res_24bit, summator_3byte_2_res_24bit, summator_3byte_3_res_24bit;
  wire [23:10] res_read_out_num;

  or or_1 (or_1_out, is_first_tact, is_zero_tact);
  not not_1 (not_1_out, or_1_out);
  // Transmission_Gate #(.width(16)) transmission_1: pin names not known; wires that end beside it: transmission_1_p1, or_1_out, not_1_out, IO_DATA_IN
  if_16bit if_16bit_1 (
    .VALUE_TRUE(spec_case_read_out_num[15:0]), .EXPRESSION(is_spec_case),
    .VALUE_FALSE({1'b0, res_exp[4:0], mant_res}), .RESULT(transmission_1_p1));
  Transistor #(.width(16)) transistor_1 (.in(IO_DATA_IN), .out(transistor_1_out), .gate(not_2_out));
  not not_2 (not_2_out[0], is_first_tact);
  counter COUNTER_TACT (.C(CLK), .ENABLE(ENABLE), .VALUE_4bit(COUNTER_TACT_value_4bit));
  assign bit_extender_1_out = {{8{1'b0}}, spec_case};  // Bit_Extender bit_extender_1
  assign bit_extender_2_out = {{20{1'b0}}, COUNTER_TACT_value_4bit};  // Bit_Extender bit_extender_2
  not not_3 (not_3_out, CLK);
  not not_4 (not_4_out, CLK);
  and and_1 (and_1_out, not_4_out, is_first_tact);
  and and_2 (and_2_out, is_first_tact, CLK);
  and and_3 (and_3_out, not_3_out, is_first_tact);
  and and_4 (and_4_out, is_first_tact, CLK);
  // NoConnect on comporator_3byte_1_num1_greater
  comporator_3byte comporator_3byte_1 (
    .NUM1(bit_extender_2_out), .NUM2({24{1'b0}}), .NUM1_GREATER(comporator_3byte_1_num1_greater),
    .EQUAL(is_zero_tact));
  // NoConnect on comporator_3byte_2_num1_greater
  comporator_3byte comporator_3byte_2 (
    .NUM1(bit_extender_2_out), .NUM2(24'h1), .NUM1_GREATER(comporator_3byte_2_num1_greater),
    .EQUAL(is_first_tact));
  // NoConnect on comporator_3byte_3_num1_greater
  comporator_3byte comporator_3byte_3 (
    .NUM1(bit_extender_2_out), .NUM2(24'hc), .NUM1_GREATER(comporator_3byte_3_num1_greater),
    .EQUAL(is_12_tact));
  parsing parsing_1 (
    .NUM_16bit(transistor_1_out), .MANT_10bit(parsing_1_mant_10bit), .EXP_5bit(parsing_1_exp_5bit),
    .SIGN(parsing_1_sign[15]));
  memory_3byte exp_read (.NUM_24bit(exp_write_out_num), .C(and_1_out), .ENABLE(ENABLE), .OUT_NUM(res_exp));
  memory_3byte exp_write (
    .NUM_24bit(if_0_than_exp_0_result), .C(and_2_out), .ENABLE(ENABLE), .OUT_NUM(exp_write_out_num));
  memory_3byte spec_case_read (
    .NUM_24bit(spec_case_write_out_num), .C(and_3_out), .ENABLE(ENABLE), .OUT_NUM(spec_case_read_out_num));
  memory_3byte spec_case_write (
    .NUM_24bit(bit_extender_1_out), .C(and_4_out), .ENABLE(ENABLE), .OUT_NUM(spec_case_write_out_num));
  if_24bit if_0_than_exp_0 (
    .VALUE_TRUE({24{1'b0}}), .EXPRESSION(is_pos_zero_1_result), .VALUE_FALSE(install_data_1_res_exp),
    .RESULT(if_0_than_exp_0_result));
  is_pos_zero is_pos_zero_1 (
    .SIGN(1'b0), .EXP_5bit(parsing_1_exp_5bit), .MANT_10bit(parsing_1_mant_10bit),
    .RESULT(is_pos_zero_1_result));
  is_pos_inf is_pos_inf_1 (
    .SIGN(parsing_1_sign[15]), .EXP_5bit(parsing_1_exp_5bit), .MANT_10bit(parsing_1_mant_10bit),
    .RESULT(is_pos_inf_1_result));
  is_neg_zero is_neg_zero_1 (
    .SIGN(parsing_1_sign[15]), .EXP_5bit(parsing_1_exp_5bit), .MANT_10bit(parsing_1_mant_10bit),
    .RESULT(is_neg_zero_1_result));
  it_is_NaN it_is_nan_1 (.EXP_5bit(parsing_1_exp_5bit), .MANT_10bit(parsing_1_mant_10bit), .RESULT(is_NaN_t));
  is_neg_num is_neg_num_1 (
    .SIGN(parsing_1_sign[15]), .EXP_5bit(parsing_1_exp_5bit), .MANT_10bit(parsing_1_mant_10bit),
    .RESULT(is_qNaN));
  install_data install_data_1 (
    .EXP_5bit(parsing_1_exp_5bit), .MANT_10bit(parsing_1_mant_10bit), .RES_MANT(install_data_1_res_mant),
    .RES_EXP(install_data_1_res_exp));
  or or_2 (or_2_out, is_pos_inf_1_result, is_neg_zero_1_result, is_NaN_t, is_qNaN);
  not not_5 (not_5_out, is_neg_zero_1_result);
  calmed_down_NaN calmed_down_nan_1 (
    .Num_16bit({parsing_1_sign[15], parsing_1_exp_5bit, parsing_1_mant_10bit}),
    .result(calmed_down_nan_1_result));
  if_24bit if_24bit_1 (
    .VALUE_TRUE(install_data_1_res_mant), .EXPRESSION(is_first_tact), .VALUE_FALSE(NUM_WRITE_out_num),
    .RESULT(if_24bit_1_result));
  or or_3 (or_3_out, is_NaN_t, is_qNaN);
  and and_5 (and_5_out, not_5_out, or_3_out);
  if_16bit if_16bit_2 (
    .VALUE_TRUE(calmed_down_nan_1_result), .EXPRESSION(is_NaN_t),
    .VALUE_FALSE({parsing_1_sign[15], parsing_1_exp_5bit, parsing_1_mant_10bit}), .RESULT(if_16bit_2_result));
  not not_6 (not_6_out, CLK);
  quite_Nan quite_nan_1 (.QNAN(quite_nan_1_qnan));
  memory_3byte NUM_READ (.NUM_24bit(if_24bit_1_result), .C(CLK), .ENABLE(ENABLE), .OUT_NUM(NUM_READ_out_num));
  memory_3byte NUM_WRITE (
    .NUM_24bit(left_shift_2_res_24bit), .C(not_6_out), .ENABLE(ENABLE), .OUT_NUM(NUM_WRITE_out_num));
  not not_7 (not_7_out, is_first_tact);
  RSC_trigger rsc_trigger_1 (
    .R(1'b0), .C(CLK), .S(and_5_out), .ENABLE(ENABLE), .Q(rsc_trigger_1_q), .not_Q(rsc_trigger_1_not_q));
  // NoConnect on rsc_trigger_1_not_q
  RSC_trigger rsc_trigger_2 (
    .R(1'b0), .C(CLK), .S(is_pos_inf_1_result), .ENABLE(ENABLE), .Q(rsc_trigger_2_q),
    .not_Q(rsc_trigger_2_not_q));
  // NoConnect on rsc_trigger_2_not_q
  or or_4 (or_4_out, or_2_out, is_12_tact);
  and and_6 (IS_NAN, not_7_out, rsc_trigger_1_q);
  not not_8 (not_8_out, rsc_trigger_1_q);
  and and_7 (IS_PINF, not_8_out, not_7_out, rsc_trigger_2_q);
  if_16bit if_16bit_3 (
    .VALUE_TRUE(quite_nan_1_qnan), .EXPRESSION(is_qNaN), .VALUE_FALSE(if_16bit_2_result),
    .RESULT(if_16bit_3_result));
  left_shift left_shift_1 (.NUM_24bit(NUM_READ_out_num), .RES_24bit(left_shift_1_res_24bit));
  RSC_trigger rsc_trigger_3 (
    .R(1'b0), .C(CLK), .S(or_4_out), .ENABLE(ENABLE), .Q(rsc_trigger_3_q), .not_Q(rsc_trigger_3_not_q));
  // NoConnect on rsc_trigger_3_not_q
  not not_9 (not_9_out, rsc_trigger_3_q);
  left_shift left_shift_2 (.NUM_24bit(left_shift_1_res_24bit), .RES_24bit(left_shift_2_res_24bit));
  and and_8 (and_8_out, is_first_tact, rsc_trigger_3_q);
  and and_9 (and_9_out, not_9_out, CLK);
  not not_10 (not_10_out, is_first_tact);
  RSC_trigger rsc_trigger_4 (
    .R(1'b0), .C(CLK), .S(and_8_out), .ENABLE(ENABLE), .Q(is_spec_case), .not_Q(rsc_trigger_4_not_q));
  // NoConnect on rsc_trigger_4_not_q
  if_16bit if_16bit_4 (
    .VALUE_TRUE(if_16bit_3_result), .EXPRESSION(and_8_out), .VALUE_FALSE({16{1'b0}}), .RESULT(spec_case));
  and and_10 (RESULT, rsc_trigger_3_q, not_10_out);
  not not_11 (not_11_out, and_9_out);
  not not_12 (not_12_out, and_9_out);
  memory_3byte res_read (
    .NUM_24bit(res_write_out_num), .C(and_9_out), .ENABLE(ENABLE), .OUT_NUM({res_read_out_num, mant_res}));
  memory_3byte res_write (.NUM_24bit(if_24bit_2_result), .C(not_11_out), .ENABLE(ENABLE), .OUT_NUM(res_write_out_num));
  memory_3byte remainder_read (
    .NUM_24bit(remainder_write_out_num), .C(and_9_out), .ENABLE(ENABLE), .OUT_NUM(remainder_read_out_num));
  memory_3byte remainder_write (
    .NUM_24bit(if_24bit_3_result), .C(not_12_out), .ENABLE(ENABLE), .OUT_NUM(remainder_write_out_num));
  left_shift left_shift_3 (.NUM_24bit({res_read_out_num, mant_res}), .RES_24bit(left_shift_3_res_24bit));
  left_shift left_shift_4 (.NUM_24bit(remainder_read_out_num), .RES_24bit(left_shift_4_res_24bit));
  assign bit_extender_3_out = {{22{1'b0}}, NUM_READ_out_num[11:10]};  // Bit_Extender bit_extender_3
  left_shift left_shift_5 (.NUM_24bit(left_shift_4_res_24bit), .RES_24bit(left_shift_5_res_24bit));
  left_shift left_shift_6 (.NUM_24bit(left_shift_3_res_24bit), .RES_24bit(left_shift_6_res_24bit));
  summator_3byte summator_3byte_1 (
    .X_24bit(left_shift_3_res_24bit), .Y_24bit(24'h1), .RES_24bit(summator_3byte_1_res_24bit));
  summator_3byte summator_3byte_2 (
    .X_24bit(bit_extender_3_out), .Y_24bit(left_shift_5_res_24bit), .RES_24bit(summator_3byte_2_res_24bit));
  summator_3byte summator_3byte_3 (
    .X_24bit(left_shift_6_res_24bit), .Y_24bit(24'h1), .RES_24bit(summator_3byte_3_res_24bit));
  comporator_3byte comporator_3byte_4 (
    .NUM1(summator_3byte_2_res_24bit), .NUM2(summator_3byte_3_res_24bit),
    .NUM1_GREATER(comporator_3byte_4_num1_greater), .EQUAL(comporator_3byte_4_equal));
  or or_5 (or_5_out, comporator_3byte_4_num1_greater, comporator_3byte_4_equal);
  substractor_3byte substractor_3byte_1 (
    .X_24bit(summator_3byte_2_res_24bit), .Y_24bit(summator_3byte_3_res_24bit),
    .RES_24bit(substractor_3byte_1_res_24bit));
  if_24bit if_24bit_2 (
    .VALUE_TRUE(summator_3byte_1_res_24bit), .EXPRESSION(or_5_out), .VALUE_FALSE(left_shift_3_res_24bit),
    .RESULT(if_24bit_2_result));
  if_24bit if_24bit_3 (
    .VALUE_TRUE(substractor_3byte_1_res_24bit), .EXPRESSION(or_5_out),
    .VALUE_FALSE(summator_3byte_2_res_24bit), .RESULT(if_24bit_3_result));
  // Pins of 1 and 16 bits meet at not_2_out

  assign IO_DATA_OUT = IO_DATA_IN;
  assign IS_NINF = 1'b0;

  // Other names for the same wires on the sheet: enble = ENABLE; synch = CLK
endmodule

module full_substracter (
  input  X,
  input  Y,
  input  B_in,
  output D,
  output B_out
);

  wire and_1_out, and_2_out, not_1_out, not_2_out, xor_1_out;

  not not_1 (not_1_out, X);
  xor xor_1 (xor_1_out, X, Y);
  and and_1 (and_1_out, not_1_out, Y);
  not not_2 (not_2_out, xor_1_out);
  and and_2 (and_2_out, B_in, not_2_out);
  xor xor_2 (D, xor_1_out, B_in);
  or or_1 (B_out, and_2_out, and_1_out);
endmodule

module substractor_byte (
  input  [7:0] X_8bit,
  input  [7:0] Y_8bit,
  input  BORROW_IN,
  output [7:0] RESULT_8bit,
  output BORROW_OUT
);

  wire full_substracter_1_b_out, full_substracter_2_b_out, full_substracter_3_b_out,
       full_substracter_4_b_out, full_substracter_5_b_out, full_substracter_6_b_out, full_substracter_7_b_out;

  full_substracter full_substracter_1 (
    .X(X_8bit[0]), .Y(Y_8bit[0]), .B_in(BORROW_IN), .D(RESULT_8bit[0]), .B_out(full_substracter_1_b_out));
  full_substracter full_substracter_2 (
    .X(X_8bit[1]), .Y(Y_8bit[1]), .B_in(full_substracter_1_b_out), .D(RESULT_8bit[1]),
    .B_out(full_substracter_2_b_out));
  full_substracter full_substracter_3 (
    .X(X_8bit[2]), .Y(Y_8bit[2]), .B_in(full_substracter_2_b_out), .D(RESULT_8bit[2]),
    .B_out(full_substracter_3_b_out));
  full_substracter full_substracter_4 (
    .X(X_8bit[3]), .Y(Y_8bit[3]), .B_in(full_substracter_3_b_out), .D(RESULT_8bit[3]),
    .B_out(full_substracter_4_b_out));
  full_substracter full_substracter_5 (
    .X(X_8bit[4]), .Y(Y_8bit[4]), .B_in(full_substracter_4_b_out), .D(RESULT_8bit[4]),
    .B_out(full_substracter_5_b_out));
  full_substracter full_substracter_6 (
    .X(X_8bit[5]), .Y(Y_8bit[5]), .B_in(full_substracter_5_b_out), .D(RESULT_8bit[5]),
    .B_out(full_substracter_6_b_out));
  full_substracter full_substracter_7 (
    .X(X_8bit[6]), .Y(Y_8bit[6]), .B_in(full_substracter_6_b_out), .D(RESULT_8bit[6]),
    .B_out(full_substracter_7_b_out));
  full_substracter full_substracter_8 (
    .X(X_8bit[7]), .Y(Y_8bit[7]), .B_in(full_substracter_7_b_out), .D(RESULT_8bit[7]), .B_out(BORROW_OUT));
endmodule

module substractor_3byte (
  input  [23:0] X_24bit,
  input  [23:0] Y_24bit,
  output [23:0] RES_24bit
);

  wire substractor_byte_1_borrow_out, substractor_byte_2_borrow_out, substractor_byte_3_borrow_out;

  substractor_byte substractor_byte_1 (
    .X_8bit(X_24bit[7:0]), .Y_8bit(Y_24bit[7:0]), .BORROW_IN(1'b0), .RESULT_8bit(RES_24bit[7:0]),
    .BORROW_OUT(substractor_byte_1_borrow_out));
  substractor_byte substractor_byte_2 (
    .X_8bit(X_24bit[15:8]), .Y_8bit(Y_24bit[15:8]), .BORROW_IN(substractor_byte_1_borrow_out),
    .RESULT_8bit(RES_24bit[15:8]), .BORROW_OUT(substractor_byte_2_borrow_out));
  substractor_byte substractor_byte_3 (
    .X_8bit(X_24bit[23:16]), .Y_8bit(Y_24bit[23:16]), .BORROW_IN(substractor_byte_2_borrow_out),
    .RESULT_8bit(RES_24bit[23:16]), .BORROW_OUT(substractor_byte_3_borrow_out));
  // NoConnect on substractor_byte_3_borrow_out
endmodule

module comporator_bit (
  input  Bit_1,
  input  Bit_2,
  input  PREV_GT,
  input  PREV_EQ,
  output GREATER,
  output EQUAL
);

  wire and_1_out, not_1_out, xnor_1_out;

  not not_1 (not_1_out, Bit_2);
  xnor xnor_1 (xnor_1_out, Bit_1, Bit_2);
  and and_1 (and_1_out, Bit_1, not_1_out, PREV_EQ);
  or or_1 (GREATER, and_1_out, PREV_GT);
  and and_2 (EQUAL, xnor_1_out, PREV_EQ);
endmodule

module comporator_byte (
  input  [7:0] X_8bit,
  input  [7:0] Y_8bit,
  input  PREV_X_GREATER,
  input  PREV_EQUAL,
  output X_GREATER,
  output EQUAL
);

  wire comporator_bit_2_equal, comporator_bit_2_greater, comporator_bit_3_equal, comporator_bit_3_greater,
       comporator_bit_4_equal, comporator_bit_4_greater, comporator_bit_5_equal, comporator_bit_5_greater,
       comporator_bit_6_equal, comporator_bit_6_greater, comporator_bit_7_equal, comporator_bit_7_greater,
       comporator_bit_8_equal, comporator_bit_8_greater;

  comporator_bit comporator_bit_1 (
    .Bit_1(X_8bit[0]), .Bit_2(Y_8bit[0]), .PREV_GT(comporator_bit_2_greater),
    .PREV_EQ(comporator_bit_2_equal), .GREATER(X_GREATER), .EQUAL(EQUAL));
  comporator_bit comporator_bit_2 (
    .Bit_1(X_8bit[1]), .Bit_2(Y_8bit[1]), .PREV_GT(comporator_bit_3_greater),
    .PREV_EQ(comporator_bit_3_equal), .GREATER(comporator_bit_2_greater), .EQUAL(comporator_bit_2_equal));
  comporator_bit comporator_bit_3 (
    .Bit_1(X_8bit[2]), .Bit_2(Y_8bit[2]), .PREV_GT(comporator_bit_4_greater),
    .PREV_EQ(comporator_bit_4_equal), .GREATER(comporator_bit_3_greater), .EQUAL(comporator_bit_3_equal));
  comporator_bit comporator_bit_4 (
    .Bit_1(X_8bit[3]), .Bit_2(Y_8bit[3]), .PREV_GT(comporator_bit_5_greater),
    .PREV_EQ(comporator_bit_5_equal), .GREATER(comporator_bit_4_greater), .EQUAL(comporator_bit_4_equal));
  comporator_bit comporator_bit_5 (
    .Bit_1(X_8bit[4]), .Bit_2(Y_8bit[4]), .PREV_GT(comporator_bit_6_greater),
    .PREV_EQ(comporator_bit_6_equal), .GREATER(comporator_bit_5_greater), .EQUAL(comporator_bit_5_equal));
  comporator_bit comporator_bit_6 (
    .Bit_1(X_8bit[5]), .Bit_2(Y_8bit[5]), .PREV_GT(comporator_bit_7_greater),
    .PREV_EQ(comporator_bit_7_equal), .GREATER(comporator_bit_6_greater), .EQUAL(comporator_bit_6_equal));
  comporator_bit comporator_bit_7 (
    .Bit_1(X_8bit[6]), .Bit_2(Y_8bit[6]), .PREV_GT(comporator_bit_8_greater),
    .PREV_EQ(comporator_bit_8_equal), .GREATER(comporator_bit_7_greater), .EQUAL(comporator_bit_7_equal));
  comporator_bit comporator_bit_8 (
    .Bit_1(X_8bit[7]), .Bit_2(Y_8bit[7]), .PREV_GT(PREV_X_GREATER), .PREV_EQ(PREV_EQUAL),
    .GREATER(comporator_bit_8_greater), .EQUAL(comporator_bit_8_equal));
endmodule

module comporator_3byte (
  input  [23:0] NUM1,
  input  [23:0] NUM2,
  output NUM1_GREATER,
  output EQUAL
);

  wire comporator_byte_2_equal, comporator_byte_2_x_greater, comporator_byte_3_equal,
       comporator_byte_3_x_greater;

  comporator_byte comporator_byte_1 (
    .X_8bit(NUM1[7:0]), .Y_8bit(NUM2[7:0]), .PREV_X_GREATER(comporator_byte_2_x_greater),
    .PREV_EQUAL(comporator_byte_2_equal), .X_GREATER(NUM1_GREATER), .EQUAL(EQUAL));
  comporator_byte comporator_byte_2 (
    .X_8bit(NUM1[15:8]), .Y_8bit(NUM2[15:8]), .PREV_X_GREATER(comporator_byte_3_x_greater),
    .PREV_EQUAL(comporator_byte_3_equal), .X_GREATER(comporator_byte_2_x_greater),
    .EQUAL(comporator_byte_2_equal));
  comporator_byte comporator_byte_3 (
    .X_8bit(NUM1[23:16]), .Y_8bit(NUM2[23:16]), .PREV_X_GREATER(1'b0), .PREV_EQUAL(1'b1),
    .X_GREATER(comporator_byte_3_x_greater), .EQUAL(comporator_byte_3_equal));
endmodule

module RS_trigger (
  input  R,
  input  S,
  input  ENABLE,
  output Q,
  output not_Q
);

  wire nor_2_out, not_1_out, or_1_out, por_1_out;

  not not_1 (not_1_out, ENABLE);
  POR por_1 (.out(por_1_out));
  nor nor_1 (Q, R, not_Q);
  nor nor_2 (nor_2_out, Q, S);
  or or_1 (or_1_out, not_1_out, por_1_out);
  or or_2 (not_Q, nor_2_out, or_1_out);
endmodule

module RSC_trigger (
  input  R,
  input  C,
  input  S,
  input  ENABLE,
  output Q,
  output not_Q
);

  wire and_1_out, and_2_out;

  and and_1 (and_1_out, R, C);
  and and_2 (and_2_out, C, S);
  RS_trigger rs_trigger_1 (.R(and_1_out), .S(and_2_out), .ENABLE(ENABLE), .Q(Q), .not_Q(not_Q));
endmodule

module D_trigger (
  input  C,
  input  D,
  input  ENABLE,
  output Q,
  output not_Q
);

  wire not_1_out;

  not not_1 (not_1_out, D);
  RSC_trigger rsc_trigger_1 (.R(not_1_out), .C(C), .S(D), .ENABLE(ENABLE), .Q(Q), .not_Q(not_Q));
endmodule

module jk_trigger (
  input  K,
  input  C,
  input  J,
  input  ENABLE,
  output Q,
  output not_Q
);

  wire and_1_out, and_2_out, not_1_out, rsc_trigger_1_not_q, rsc_trigger_1_q;

  and and_1 (and_1_out, Q, K);
  and and_2 (and_2_out, J, not_Q);
  not not_1 (not_1_out, C);
  RSC_trigger rsc_trigger_1 (
    .R(and_1_out), .C(C), .S(and_2_out), .ENABLE(ENABLE), .Q(rsc_trigger_1_q), .not_Q(rsc_trigger_1_not_q));
  RSC_trigger rsc_trigger_2 (
    .R(rsc_trigger_1_not_q), .C(not_1_out), .S(rsc_trigger_1_q), .ENABLE(ENABLE), .Q(Q), .not_Q(not_Q));
endmodule

module summator_bit (
  input  CARRY_IN,
  input  bit_1,
  input  bit_2,
  output RES,
  output CARRY_OUT
);

  wire and_1_out, and_2_out, xor_1_out;

  xor xor_1 (xor_1_out, bit_1, bit_2);
  and and_1 (and_1_out, bit_1, bit_2);
  xor xor_2 (RES, CARRY_IN, xor_1_out);
  and and_2 (and_2_out, CARRY_IN, xor_1_out);
  or or_1 (CARRY_OUT, and_2_out, and_1_out);
endmodule

module summator_byte (
  input  CARRY_IN,
  input  [7:0] X_8bit,
  input  [7:0] Y_8bit,
  output [7:0] RES_8bit,
  output CARRY_OUT
);

  wire summator_bit_1_carry_out, summator_bit_2_carry_out, summator_bit_3_carry_out,
       summator_bit_4_carry_out, summator_bit_5_carry_out, summator_bit_6_carry_out, summator_bit_7_carry_out;

  summator_bit summator_bit_1 (
    .CARRY_IN(CARRY_IN), .bit_1(X_8bit[0]), .bit_2(Y_8bit[0]), .RES(RES_8bit[0]),
    .CARRY_OUT(summator_bit_1_carry_out));
  summator_bit summator_bit_2 (
    .CARRY_IN(summator_bit_1_carry_out), .bit_1(X_8bit[1]), .bit_2(Y_8bit[1]), .RES(RES_8bit[1]),
    .CARRY_OUT(summator_bit_2_carry_out));
  summator_bit summator_bit_3 (
    .CARRY_IN(summator_bit_2_carry_out), .bit_1(X_8bit[2]), .bit_2(Y_8bit[2]), .RES(RES_8bit[2]),
    .CARRY_OUT(summator_bit_3_carry_out));
  summator_bit summator_bit_4 (
    .CARRY_IN(summator_bit_3_carry_out), .bit_1(X_8bit[3]), .bit_2(Y_8bit[3]), .RES(RES_8bit[3]),
    .CARRY_OUT(summator_bit_4_carry_out));
  summator_bit summator_bit_5 (
    .CARRY_IN(summator_bit_4_carry_out), .bit_1(X_8bit[4]), .bit_2(Y_8bit[4]), .RES(RES_8bit[4]),
    .CARRY_OUT(summator_bit_5_carry_out));
  summator_bit summator_bit_6 (
    .CARRY_IN(summator_bit_5_carry_out), .bit_1(X_8bit[5]), .bit_2(Y_8bit[5]), .RES(RES_8bit[5]),
    .CARRY_OUT(summator_bit_6_carry_out));
  summator_bit summator_bit_7 (
    .CARRY_IN(summator_bit_6_carry_out), .bit_1(X_8bit[6]), .bit_2(Y_8bit[6]), .RES(RES_8bit[6]),
    .CARRY_OUT(summator_bit_7_carry_out));
  summator_bit summator_bit_8 (
    .CARRY_IN(summator_bit_7_carry_out), .bit_1(X_8bit[7]), .bit_2(Y_8bit[7]), .RES(RES_8bit[7]),
    .CARRY_OUT(CARRY_OUT));
endmodule

module summator_3byte (
  input  [23:0] X_24bit,
  input  [23:0] Y_24bit,
  output [23:0] RES_24bit
);

  wire summator_byte_1_carry_out, summator_byte_2_carry_out, summator_byte_3_carry_out;

  summator_byte summator_byte_1 (
    .CARRY_IN(1'b0), .X_8bit(X_24bit[7:0]), .Y_8bit(Y_24bit[7:0]), .RES_8bit(RES_24bit[7:0]),
    .CARRY_OUT(summator_byte_1_carry_out));
  summator_byte summator_byte_2 (
    .CARRY_IN(summator_byte_1_carry_out), .X_8bit(X_24bit[15:8]), .Y_8bit(Y_24bit[15:8]),
    .RES_8bit(RES_24bit[15:8]), .CARRY_OUT(summator_byte_2_carry_out));
  summator_byte summator_byte_3 (
    .CARRY_IN(summator_byte_2_carry_out), .X_8bit(X_24bit[23:16]), .Y_8bit(Y_24bit[23:16]),
    .RES_8bit(RES_24bit[23:16]), .CARRY_OUT(summator_byte_3_carry_out));
  // NoConnect on summator_byte_3_carry_out
endmodule

module parsing (
  input  [15:0] NUM_16bit,
  output [9:0] MANT_10bit,
  output [4:0] EXP_5bit,
  output SIGN
);


  assign EXP_5bit = NUM_16bit[14:10];
  assign MANT_10bit = NUM_16bit[9:0];
  assign SIGN = NUM_16bit[15];
endmodule

module is_pos_inf (
  input  SIGN,
  input  [4:0] EXP_5bit,
  input  [9:0] MANT_10bit,
  output RESULT
);

  wire comporator_3byte_1_equal, comporator_3byte_1_num1_greater, comporator_3byte_2_equal,
       comporator_3byte_2_num1_greater, not_1_out;
  wire [23:0] bit_extender_1_out, bit_extender_2_out;

  assign bit_extender_1_out = {{19{1'b0}}, EXP_5bit};  // Bit_Extender bit_extender_1
  assign bit_extender_2_out = {{14{1'b0}}, MANT_10bit};  // Bit_Extender bit_extender_2
  not not_1 (not_1_out, SIGN);
  // NoConnect on comporator_3byte_1_num1_greater
  comporator_3byte comporator_3byte_1 (
    .NUM1(bit_extender_1_out), .NUM2(24'h1f), .NUM1_GREATER(comporator_3byte_1_num1_greater),
    .EQUAL(comporator_3byte_1_equal));
  // NoConnect on comporator_3byte_2_num1_greater
  comporator_3byte comporator_3byte_2 (
    .NUM1(bit_extender_2_out), .NUM2({24{1'b0}}), .NUM1_GREATER(comporator_3byte_2_num1_greater),
    .EQUAL(comporator_3byte_2_equal));
  and and_1 (RESULT, not_1_out, comporator_3byte_1_equal, comporator_3byte_2_equal);
endmodule

module is_neg_zero (
  input  SIGN,
  input  [4:0] EXP_5bit,
  input  [9:0] MANT_10bit,
  output RESULT
);

  wire comporator_3byte_1_equal, comporator_3byte_1_num1_greater, comporator_3byte_2_equal,
       comporator_3byte_2_num1_greater;
  wire [23:0] bit_extender_1_out, bit_extender_2_out;

  assign bit_extender_1_out = {{19{1'b0}}, EXP_5bit};  // Bit_Extender bit_extender_1
  assign bit_extender_2_out = {{14{1'b0}}, MANT_10bit};  // Bit_Extender bit_extender_2
  // NoConnect on comporator_3byte_1_num1_greater
  comporator_3byte comporator_3byte_1 (
    .NUM1(bit_extender_1_out), .NUM2({24{1'b0}}), .NUM1_GREATER(comporator_3byte_1_num1_greater),
    .EQUAL(comporator_3byte_1_equal));
  // NoConnect on comporator_3byte_2_num1_greater
  comporator_3byte comporator_3byte_2 (
    .NUM1(bit_extender_2_out), .NUM2({24{1'b0}}), .NUM1_GREATER(comporator_3byte_2_num1_greater),
    .EQUAL(comporator_3byte_2_equal));
  and and_1 (RESULT, SIGN, comporator_3byte_1_equal, comporator_3byte_2_equal);
endmodule

module is_pos_zero (
  input  SIGN,
  input  [4:0] EXP_5bit,
  input  [9:0] MANT_10bit,
  output RESULT
);

  wire comporator_3byte_1_equal, comporator_3byte_1_num1_greater, comporator_3byte_2_equal,
       comporator_3byte_2_num1_greater, not_1_out;
  wire [23:0] bit_extender_1_out, bit_extender_2_out;

  assign bit_extender_1_out = {{19{1'b0}}, EXP_5bit};  // Bit_Extender bit_extender_1
  assign bit_extender_2_out = {{14{1'b0}}, MANT_10bit};  // Bit_Extender bit_extender_2
  // NoConnect on comporator_3byte_1_num1_greater
  comporator_3byte comporator_3byte_1 (
    .NUM1(bit_extender_1_out), .NUM2({24{1'b0}}), .NUM1_GREATER(comporator_3byte_1_num1_greater),
    .EQUAL(comporator_3byte_1_equal));
  // NoConnect on comporator_3byte_2_num1_greater
  comporator_3byte comporator_3byte_2 (
    .NUM1(bit_extender_2_out), .NUM2({24{1'b0}}), .NUM1_GREATER(comporator_3byte_2_num1_greater),
    .EQUAL(comporator_3byte_2_equal));
  not not_1 (not_1_out, SIGN);
  and and_1 (RESULT, not_1_out, comporator_3byte_1_equal, comporator_3byte_2_equal);
endmodule

module quite_Nan (
  output [15:0] QNAN
);


  assign QNAN = 16'hfe00;
endmodule

module calmed_down_NaN (
  input  [15:0] Num_16bit,
  output [15:0] result
);


  assign result = {Num_16bit[15:10], 1'b1, Num_16bit[8:0]};
endmodule

module it_is_NaN (
  input  [4:0] EXP_5bit,
  input  [9:0] MANT_10bit,
  output RESULT
);

  wire comporator_3byte_1_equal, comporator_3byte_1_num1_greater, comporator_3byte_2_equal,
       comporator_3byte_2_num1_greater, not_1_out;
  wire [23:0] bit_extender_1_out, bit_extender_2_out;

  assign bit_extender_1_out = {{19{1'b0}}, EXP_5bit};  // Bit_Extender bit_extender_1
  assign bit_extender_2_out = {{14{1'b0}}, MANT_10bit};  // Bit_Extender bit_extender_2
  // NoConnect on comporator_3byte_1_num1_greater
  comporator_3byte comporator_3byte_1 (
    .NUM1(bit_extender_1_out), .NUM2(24'h1f), .NUM1_GREATER(comporator_3byte_1_num1_greater),
    .EQUAL(comporator_3byte_1_equal));
  // NoConnect on comporator_3byte_2_num1_greater
  comporator_3byte comporator_3byte_2 (
    .NUM1(bit_extender_2_out), .NUM2({24{1'b0}}), .NUM1_GREATER(comporator_3byte_2_num1_greater),
    .EQUAL(comporator_3byte_2_equal));
  not not_1 (not_1_out, comporator_3byte_2_equal);
  and and_1 (RESULT, comporator_3byte_1_equal, not_1_out);
endmodule

module is_neg_num (
  input  SIGN,
  input  [4:0] EXP_5bit,
  input  [9:0] MANT_10bit,
  output RESULT
);

  wire is_neg_zero_1_result, it_is_nan_1_result, not_1_out, not_2_out;

  is_neg_zero is_neg_zero_1 (.SIGN(SIGN), .EXP_5bit(EXP_5bit), .MANT_10bit(MANT_10bit), .RESULT(is_neg_zero_1_result));
  it_is_NaN it_is_nan_1 (.EXP_5bit(EXP_5bit), .MANT_10bit(MANT_10bit), .RESULT(it_is_nan_1_result));
  not not_1 (not_1_out, is_neg_zero_1_result);
  not not_2 (not_2_out, it_is_nan_1_result);
  and and_1 (RESULT, SIGN, not_1_out, not_2_out);
endmodule

module if_16bit (
  input  [15:0] VALUE_TRUE,
  input  EXPRESSION,
  input  [15:0] VALUE_FALSE,
  output [15:0] RESULT
);

  wire not_1_out, not_2_out;

  not not_1 (not_1_out, EXPRESSION);
  not not_2 (not_2_out, EXPRESSION);
  // Transmission_Gate #(.width(16)) transmission_1: pin names not known; wires that end beside it: VALUE_TRUE, not_1_out, EXPRESSION, RESULT
  // Transmission_Gate #(.width(16)) transmission_2: pin names not known; wires that end beside it: VALUE_FALSE, EXPRESSION, not_2_out, RESULT
endmodule

module if_24bit (
  input  [23:0] VALUE_TRUE,
  input  EXPRESSION,
  input  [23:0] VALUE_FALSE,
  output [23:0] RESULT
);

  wire not_1_out, not_2_out;

  not not_1 (not_1_out, EXPRESSION);
  not not_2 (not_2_out, EXPRESSION);
  // Transmission_Gate #(.width(24)) transmission_1: pin names not known; wires that end beside it: VALUE_TRUE, not_1_out, EXPRESSION, RESULT
  // Transmission_Gate #(.width(24)) transmission_2: pin names not known; wires that end beside it: VALUE_FALSE, EXPRESSION, not_2_out, RESULT
endmodule

module install_data (
  input  [4:0] EXP_5bit,
  input  [9:0] MANT_10bit,
  output [23:0] RES_MANT,
  output [23:0] RES_EXP
);

  wire comporator_3byte_1_num1_greater, comporator_3byte_2_equal, comporator_3byte_2_num1_greater, is_exp_0,
       not_1_out;
  wire [23:0] bit_extender_3_out, bit_extender_4_out, denorm_mant, denorm_to_norm_1_shift_exp, exp,
       if_24bit_1_result, if_24bit_3_result, left_shift_1_res_24bit, left_shift_2_res_24bit, mant,
       new_denorm_exp_1_res_exp, new_normal_exp_1_new_exp_24bit;

  assign exp = {{19{1'b0}}, EXP_5bit};  // Bit_Extender bit_extender_1
  assign mant = {{14{1'b0}}, MANT_10bit};  // Bit_Extender bit_extender_2
  denorm_to_norm denorm_to_norm_1 (
    .EXP_24bit(exp), .MANT_24bit(mant), .SHIFT_EXP(denorm_to_norm_1_shift_exp), .NEW_MANT_24bit(denorm_mant));
  assign bit_extender_3_out = {{23{1'b0}}, denorm_to_norm_1_shift_exp[0]};  // Bit_Extender bit_extender_3
  new_denorm_exp new_denorm_exp_1 (.SHIFT_EXP_24bit(denorm_to_norm_1_shift_exp), .RES_EXP(new_denorm_exp_1_res_exp));
  // NoConnect on comporator_3byte_1_num1_greater
  comporator_3byte comporator_3byte_1 (
    .NUM1(exp), .NUM2({24{1'b0}}), .NUM1_GREATER(comporator_3byte_1_num1_greater), .EQUAL(is_exp_0));
  new_normal_exp new_normal_exp_1 (.EXP_24bit(exp), .NEW_EXP_24bit(new_normal_exp_1_new_exp_24bit));
  // NoConnect on comporator_3byte_2_num1_greater
  comporator_3byte comporator_3byte_2 (
    .NUM1(bit_extender_3_out), .NUM2({24{1'b0}}), .NUM1_GREATER(comporator_3byte_2_num1_greater),
    .EQUAL(comporator_3byte_2_equal));
  not not_1 (not_1_out, comporator_3byte_2_equal);
  left_shift left_shift_1 (.NUM_24bit(denorm_mant), .RES_24bit(left_shift_1_res_24bit));
  if_24bit if_denorm_num (
    .VALUE_TRUE(new_denorm_exp_1_res_exp), .EXPRESSION(is_exp_0),
    .VALUE_FALSE(new_normal_exp_1_new_exp_24bit), .RESULT(RES_EXP));
  if_24bit if_24bit_1 (
    .VALUE_TRUE(left_shift_1_res_24bit), .EXPRESSION(not_1_out), .VALUE_FALSE(denorm_mant),
    .RESULT(if_24bit_1_result));
  assign bit_extender_4_out = {{13{1'b0}}, {1'b1, mant[9:0]}};  // Bit_Extender bit_extender_4
  left_shift left_shift_2 (.NUM_24bit(bit_extender_4_out), .RES_24bit(left_shift_2_res_24bit));
  if_24bit if_24bit_2 (
    .VALUE_TRUE(if_24bit_1_result), .EXPRESSION(is_exp_0), .VALUE_FALSE(if_24bit_3_result), .RESULT(RES_MANT));
  if_24bit if_24bit_3 (
    .VALUE_TRUE(bit_extender_4_out), .EXPRESSION(exp[0]), .VALUE_FALSE(left_shift_2_res_24bit),
    .RESULT(if_24bit_3_result));
endmodule

module new_normal_exp (
  input  [23:0] EXP_24bit,
  output [23:0] NEW_EXP_24bit
);

  wire exp_more_equal_15_equal, exp_more_equal_15_num1_greater, or_1_out, or_2_out;
  wire [23:0] if_24bit_1_result, right_shift_1_res_24bit, right_shift_2_res_24bit,
       substractor_3byte_1_res_24bit, substractor_3byte_2_res_24bit, substractor_3byte_3_res_24bit,
       substractor_3byte_4_res_24bit, summator_3byte_1_res_24bit;

  substractor_3byte substractor_3byte_1 (
    .X_24bit(EXP_24bit), .Y_24bit(24'hf), .RES_24bit(substractor_3byte_1_res_24bit));
  substractor_3byte substractor_3byte_2 (
    .X_24bit(24'hf), .Y_24bit(EXP_24bit), .RES_24bit(substractor_3byte_2_res_24bit));
  comporator_3byte exp_more_equal_15 (
    .NUM1(EXP_24bit), .NUM2(24'hf), .NUM1_GREATER(exp_more_equal_15_num1_greater),
    .EQUAL(exp_more_equal_15_equal));
  right_shift right_shift_1 (.NUM_24bit(substractor_3byte_2_res_24bit), .RES_24bit(right_shift_1_res_24bit));
  right_shift right_shift_2 (.NUM_24bit(substractor_3byte_1_res_24bit), .RES_24bit(right_shift_2_res_24bit));
  or or_1 (or_1_out, exp_more_equal_15_num1_greater, exp_more_equal_15_equal);
  summator_3byte summator_3byte_1 (
    .X_24bit(right_shift_2_res_24bit), .Y_24bit(24'hf), .RES_24bit(summator_3byte_1_res_24bit));
  substractor_3byte substractor_3byte_3 (
    .X_24bit(24'hf), .Y_24bit(right_shift_1_res_24bit), .RES_24bit(substractor_3byte_3_res_24bit));
  if_24bit if_24bit_1 (
    .VALUE_TRUE(summator_3byte_1_res_24bit), .EXPRESSION(or_1_out),
    .VALUE_FALSE(substractor_3byte_3_res_24bit), .RESULT(if_24bit_1_result));
  or or_2 (or_2_out, EXP_24bit[0], or_1_out);
  substractor_3byte substractor_3byte_4 (
    .X_24bit(if_24bit_1_result), .Y_24bit(24'h1), .RES_24bit(substractor_3byte_4_res_24bit));
  if_24bit if_exp_even_then_res_minus_1 (
    .VALUE_TRUE(if_24bit_1_result), .EXPRESSION(or_2_out), .VALUE_FALSE(substractor_3byte_4_res_24bit),
    .RESULT(NEW_EXP_24bit));

  // Other names for the same wires on the sheet: exp[23:0] = EXP_24bit
endmodule

module new_denorm_exp (
  input  [23:0] SHIFT_EXP_24bit,
  output [23:0] RES_EXP
);

  wire comporator_3byte_1_equal, comporator_3byte_1_num1_greater, not_1_out;
  wire [23:0] bit_extender_1_out, right_shift_1_res_24bit, substractor_3byte_1_res_24bit,
       substractor_3byte_2_res_24bit, summator_3byte_1_res_24bit;

  summator_3byte summator_3byte_1 (.X_24bit(SHIFT_EXP_24bit), .Y_24bit(24'he), .RES_24bit(summator_3byte_1_res_24bit));
  assign bit_extender_1_out = {{23{1'b0}}, SHIFT_EXP_24bit[0]};  // Bit_Extender bit_extender_1
  right_shift right_shift_1 (.NUM_24bit(summator_3byte_1_res_24bit), .RES_24bit(right_shift_1_res_24bit));
  // NoConnect on comporator_3byte_1_num1_greater
  comporator_3byte comporator_3byte_1 (
    .NUM1(bit_extender_1_out), .NUM2({24{1'b0}}), .NUM1_GREATER(comporator_3byte_1_num1_greater),
    .EQUAL(comporator_3byte_1_equal));
  substractor_3byte substractor_3byte_1 (
    .X_24bit(24'hf), .Y_24bit(right_shift_1_res_24bit), .RES_24bit(substractor_3byte_1_res_24bit));
  not not_1 (not_1_out, comporator_3byte_1_equal);
  substractor_3byte substractor_3byte_2 (
    .X_24bit(substractor_3byte_1_res_24bit), .Y_24bit(24'h1), .RES_24bit(substractor_3byte_2_res_24bit));
  if_24bit if_shift_odd (
    .VALUE_TRUE(substractor_3byte_2_res_24bit), .EXPRESSION(not_1_out),
    .VALUE_FALSE(substractor_3byte_1_res_24bit), .RESULT(RES_EXP));

  // Other names for the same wires on the sheet: shift[23:0] = SHIFT_EXP_24bit
endmodule

module denorm_to_norm (
  input  [23:0] EXP_24bit,
  input  [23:0] MANT_24bit,
  output [23:0] SHIFT_EXP,
  output [23:0] NEW_MANT_24bit
);

  wire comporator_3byte_1_equal, comporator_3byte_1_num1_greater;
  wire [23:0] step_denorm_1_res_mant, step_denorm_1_res_shift, step_denorm_2_res_mant,
       step_denorm_2_res_shift, step_denorm_3_res_mant, step_denorm_3_res_shift, step_denorm_4_res_mant,
       step_denorm_4_res_shift, step_denorm_5_res_mant, step_denorm_5_res_shift, step_denorm_6_res_mant,
       step_denorm_6_res_shift, step_denorm_7_res_mant, step_denorm_7_res_shift, step_denorm_8_res_mant,
       step_denorm_8_res_shift, step_denorm_9_res_mant, step_denorm_9_res_shift, step_denorm_10_res_mant,
       step_denorm_10_res_shift;

  step_denorm step_denorm_1 (
    .SHIFT_EXP_24bit({24{1'b0}}), .MANT_24bit(MANT_24bit), .RES_SHIFT(step_denorm_1_res_shift),
    .RES_MANT(step_denorm_1_res_mant));
  step_denorm step_denorm_2 (
    .SHIFT_EXP_24bit(step_denorm_9_res_shift), .MANT_24bit(step_denorm_9_res_mant),
    .RES_SHIFT(step_denorm_2_res_shift), .RES_MANT(step_denorm_2_res_mant));
  step_denorm step_denorm_3 (
    .SHIFT_EXP_24bit(step_denorm_1_res_shift), .MANT_24bit(step_denorm_1_res_mant),
    .RES_SHIFT(step_denorm_3_res_shift), .RES_MANT(step_denorm_3_res_mant));
  step_denorm step_denorm_4 (
    .SHIFT_EXP_24bit(step_denorm_2_res_shift), .MANT_24bit(step_denorm_2_res_mant),
    .RES_SHIFT(step_denorm_4_res_shift), .RES_MANT(step_denorm_4_res_mant));
  // NoConnect on comporator_3byte_1_num1_greater
  comporator_3byte comporator_3byte_1 (
    .NUM1(EXP_24bit), .NUM2({24{1'b0}}), .NUM1_GREATER(comporator_3byte_1_num1_greater),
    .EQUAL(comporator_3byte_1_equal));
  step_denorm step_denorm_5 (
    .SHIFT_EXP_24bit(step_denorm_3_res_shift), .MANT_24bit(step_denorm_3_res_mant),
    .RES_SHIFT(step_denorm_5_res_shift), .RES_MANT(step_denorm_5_res_mant));
  step_denorm step_denorm_6 (
    .SHIFT_EXP_24bit(step_denorm_4_res_shift), .MANT_24bit(step_denorm_4_res_mant),
    .RES_SHIFT(step_denorm_6_res_shift), .RES_MANT(step_denorm_6_res_mant));
  step_denorm step_denorm_7 (
    .SHIFT_EXP_24bit(step_denorm_5_res_shift), .MANT_24bit(step_denorm_5_res_mant),
    .RES_SHIFT(step_denorm_7_res_shift), .RES_MANT(step_denorm_7_res_mant));
  step_denorm step_denorm_8 (
    .SHIFT_EXP_24bit(step_denorm_6_res_shift), .MANT_24bit(step_denorm_6_res_mant),
    .RES_SHIFT(step_denorm_8_res_shift), .RES_MANT(step_denorm_8_res_mant));
  if_24bit if_exp_equal_0 (
    .VALUE_TRUE(step_denorm_10_res_mant), .EXPRESSION(comporator_3byte_1_equal), .VALUE_FALSE(MANT_24bit),
    .RESULT(NEW_MANT_24bit));
  step_denorm step_denorm_9 (
    .SHIFT_EXP_24bit(step_denorm_7_res_shift), .MANT_24bit(step_denorm_7_res_mant),
    .RES_SHIFT(step_denorm_9_res_shift), .RES_MANT(step_denorm_9_res_mant));
  step_denorm step_denorm_10 (
    .SHIFT_EXP_24bit(step_denorm_8_res_shift), .MANT_24bit(step_denorm_8_res_mant),
    .RES_SHIFT(step_denorm_10_res_shift), .RES_MANT(step_denorm_10_res_mant));
  if_24bit if_24bit_1 (
    .VALUE_TRUE(step_denorm_10_res_shift), .EXPRESSION(comporator_3byte_1_equal), .VALUE_FALSE({24{1'b0}}),
    .RESULT(SHIFT_EXP));

  // Other names for the same wires on the sheet: mant[23:0] = MANT_24bit
endmodule

module step_denorm (
  input  [23:0] SHIFT_EXP_24bit,
  input  [23:0] MANT_24bit,
  output [23:0] RES_SHIFT,
  output [23:0] RES_MANT
);

  wire not_1_out;
  wire [23:0] left_shift_1_res_24bit, summator_3byte_1_res_24bit;

  summator_3byte summator_3byte_1 (.X_24bit(SHIFT_EXP_24bit), .Y_24bit(24'h1), .RES_24bit(summator_3byte_1_res_24bit));
  left_shift left_shift_1 (.NUM_24bit(MANT_24bit), .RES_24bit(left_shift_1_res_24bit));
  not not_1 (not_1_out, MANT_24bit[10]);
  if_24bit if_10bit_mant_not_0 (
    .VALUE_TRUE(summator_3byte_1_res_24bit), .EXPRESSION(not_1_out), .VALUE_FALSE(SHIFT_EXP_24bit),
    .RESULT(RES_SHIFT));
  if_24bit if_10bit_mant_not_zero (
    .VALUE_TRUE(left_shift_1_res_24bit), .EXPRESSION(not_1_out), .VALUE_FALSE(MANT_24bit), .RESULT(RES_MANT));
endmodule

module counter (
  input  C,
  input  ENABLE,
  output [3:0] VALUE_4bit
);

  wire comporator_3byte_1_equal, comporator_3byte_1_num1_greater, jk_trigger_1_not_q, jk_trigger_2_not_q,
       jk_trigger_3_not_q, jk_trigger_4_not_q, not_1_out, not_2_out, not_3_out, not_4_out,
       rsc_trigger_1_not_q, rsc_trigger_1_q;
  wire [3:0] jk_trigger_1_q;
  wire [23:0] if_24bit_1_result, value;
  wire [23:4] if_24bit_2_result;

  not not_1 (not_1_out, C);
  jk_trigger jk_trigger_1 (
    .K(1'b1), .C(not_1_out), .J(1'b1), .ENABLE(ENABLE), .Q(jk_trigger_1_q[0]), .not_Q(jk_trigger_1_not_q));
  not not_2 (not_2_out, jk_trigger_1_not_q);
  jk_trigger jk_trigger_2 (
    .K(1'b1), .C(not_2_out), .J(1'b1), .ENABLE(ENABLE), .Q(jk_trigger_1_q[1]), .not_Q(jk_trigger_2_not_q));
  not not_3 (not_3_out, jk_trigger_2_not_q);
  // NoConnect on comporator_3byte_1_num1_greater
  comporator_3byte comporator_3byte_1 (
    .NUM1(value), .NUM2(24'hf), .NUM1_GREATER(comporator_3byte_1_num1_greater),
    .EQUAL(comporator_3byte_1_equal));
  jk_trigger jk_trigger_3 (
    .K(1'b1), .C(not_3_out), .J(1'b1), .ENABLE(ENABLE), .Q(jk_trigger_1_q[2]), .not_Q(jk_trigger_3_not_q));
  not not_4 (not_4_out, jk_trigger_3_not_q);
  if_24bit if_24bit_1 (
    .VALUE_TRUE(24'h1), .EXPRESSION(comporator_3byte_1_equal), .VALUE_FALSE({24{1'b0}}),
    .RESULT(if_24bit_1_result));
  jk_trigger jk_trigger_4 (
    .K(1'b1), .C(not_4_out), .J(1'b1), .ENABLE(ENABLE), .Q(jk_trigger_1_q[3]), .not_Q(jk_trigger_4_not_q));
  // NoConnect on jk_trigger_4_not_q
  assign value = {{20{1'b0}}, jk_trigger_1_q};  // Bit_Extender bit_extender_1
  RSC_trigger rsc_trigger_1 (
    .R(1'b0), .C(C), .S(if_24bit_1_result[0]), .ENABLE(ENABLE), .Q(rsc_trigger_1_q),
    .not_Q(rsc_trigger_1_not_q));
  // NoConnect on rsc_trigger_1_not_q
  if_24bit if_24bit_2 (
    .VALUE_TRUE(24'hf), .EXPRESSION(rsc_trigger_1_q), .VALUE_FALSE(value),
    .RESULT({if_24bit_2_result, VALUE_4bit}));

  // Other names for the same wires on the sheet: clk = C; enble = ENABLE
endmodule

module left_shift (
  input  [23:0] NUM_24bit,
  output [23:0] RES_24bit
);


  assign RES_24bit = {NUM_24bit[22:0], 1'b0};
endmodule

module right_shift (
  input  [23:0] NUM_24bit,
  output [23:0] RES_24bit
);

  assign RES_24bit = {{1{1'b0}}, NUM_24bit[23:1]};  // Bit_Extender bit_extender_1
endmodule

module memory_byte (
  input  [7:0] NUM_8bit,
  input  C,
  input  ENABLE,
  output [7:0] OUT_NUM
);

  wire d_trigger_1_not_q, d_trigger_2_not_q, d_trigger_3_not_q, d_trigger_4_not_q, d_trigger_5_not_q,
       d_trigger_6_not_q, d_trigger_7_not_q, d_trigger_8_not_q;

  D_trigger d_trigger_1 (.C(C), .D(NUM_8bit[0]), .ENABLE(ENABLE), .Q(OUT_NUM[0]), .not_Q(d_trigger_1_not_q));
  // NoConnect on d_trigger_1_not_q
  D_trigger d_trigger_2 (.C(C), .D(NUM_8bit[1]), .ENABLE(ENABLE), .Q(OUT_NUM[1]), .not_Q(d_trigger_2_not_q));
  // NoConnect on d_trigger_2_not_q
  D_trigger d_trigger_3 (.C(C), .D(NUM_8bit[2]), .ENABLE(ENABLE), .Q(OUT_NUM[2]), .not_Q(d_trigger_3_not_q));
  // NoConnect on d_trigger_3_not_q
  D_trigger d_trigger_4 (.C(C), .D(NUM_8bit[3]), .ENABLE(ENABLE), .Q(OUT_NUM[3]), .not_Q(d_trigger_4_not_q));
  // NoConnect on d_trigger_4_not_q
  D_trigger d_trigger_5 (.C(C), .D(NUM_8bit[4]), .ENABLE(ENABLE), .Q(OUT_NUM[4]), .not_Q(d_trigger_5_not_q));
  // NoConnect on d_trigger_5_not_q
  D_trigger d_trigger_6 (.C(C), .D(NUM_8bit[5]), .ENABLE(ENABLE), .Q(OUT_NUM[5]), .not_Q(d_trigger_6_not_q));
  // NoConnect on d_trigger_6_not_q
  D_trigger d_trigger_7 (.C(C), .D(NUM_8bit[6]), .ENABLE(ENABLE), .Q(OUT_NUM[6]), .not_Q(d_trigger_7_not_q));
  // NoConnect on d_trigger_7_not_q
  D_trigger d_trigger_8 (.C(C), .D(NUM_8bit[7]), .ENABLE(ENABLE), .Q(OUT_NUM[7]), .not_Q(d_trigger_8_not_q));
  // NoConnect on d_trigger_8_not_q
endmodule

module memory_3byte (
  input  [23:0] NUM_24bit,
  input  C,
  input  ENABLE,
  output [23:0] OUT_NUM
);

  memory_byte memory_byte_1 (.NUM_8bit(NUM_24bit[7:0]), .C(C), .ENABLE(ENABLE), .OUT_NUM(OUT_NUM[7:0]));
  memory_byte memory_byte_2 (.NUM_8bit(NUM_24bit[15:8]), .C(C), .ENABLE(ENABLE), .OUT_NUM(OUT_NUM[15:8]));
  memory_byte memory_byte_3 (.NUM_8bit(NUM_24bit[23:16]), .C(C), .ENABLE(ENABLE), .OUT_NUM(OUT_NUM[23:16]));
endmodule
