// Logisim project sqrt2.circ as structural Verilog: 35 circuits, main circuit main
module main (
  input  ENABLE,
  input  [15:0] IO_DATA_IN,
  output NAN,
  output PINF,
  output NINF,
  output RESULT,
  output [15:0] IO_DATA_OUT
);

  wire CLK_out;

  Clock CLK (.out(CLK_out));
  sqrt sqrt_1 (
    .CLK(CLK_out), .ENABLE(ENABLE), .IO_DATA_IN(IO_DATA_IN), .IS_NAN(NAN), .IS_PINF(PINF), .IS_NINF(NINF),
    .RESULT(RESULT), .IO_DATA_OUT(IO_DATA_OUT));
endmodule

module sqrt (
  input  CLK,
  input  ENABLE,
  input  [15:0] IO_DATA_IN,
  output IS_NAN,
  output IS_PINF,
  output IS_NINF,
  output RESULT,
  output [15:0] IO_DATA_OUT
);

  wire and_1_out, comporator_3byte_1_equal, comporator_3byte_3_equal, comporator_3byte_3_num1_greater,
       is_neg_num_1_res, is_neg_zero_1_res, is_pos_inf_1_res, it_is_nan_1_res, not_2_out, not_3_out,
       not_4_out, not_5_out, not_6_out, not_7_out, or_1_out, or_2_out, or_3_out, or_4_out;
  wire [4:0] normalization_mant_1_res_exp_5bit, parsing_1_exp_5bit;
  wire [9:0] mant_res, parsing_1_mant_10bit;
  wire [15:0] counter_1_value_16bit, not_1_out, quite_nan_1_qnan, transistor_1_out;
  wire [15:15] parsing_1_sign;
  wire [23:0] bit_extender_1_out, bit_extender_2_out, bit_extender_3_out, bit_extender_4_out,
       if_24bit_1_result, if_24bit_2_result, if_24bit_3_result, left_shift_1_res_24bit,
       left_shift_2_res_24bit, left_shift_3_res_24bit, left_shift_4_res_24bit, left_shift_5_res_24bit,
       left_shift_6_res_24bit, memory_3byte_1_out_num, memory_3byte_2_out_num, memory_3byte_3_out_num,
       new_exp_1_new_exp_24bit, normalization_mant_1_mant_24bit, remainder_read_out_num,
       remainder_write_out_num, res_write_out_num, substractor_3byte_1_res_24bit, summator_3byte_1_res_24bit,
       summator_3byte_2_res_24bit, summator_3byte_3_res_24bit;
  wire [23:10] res_read_out_num;

  // Probe on mant_res
  Transistor #(.width(16)) transistor_1 (.in(IO_DATA_IN), .out(transistor_1_out), .gate(not_1_out));
  counter counter_1 (.C(CLK), .enable(ENABLE), .value_16bit(counter_1_value_16bit));
  assign bit_extender_1_out = {{8{1'b0}}, counter_1_value_16bit};  // Bit_Extender bit_extender_1
  assign bit_extender_2_out = {{8{1'b0}}, counter_1_value_16bit};  // Bit_Extender bit_extender_2
  comporator_3byte comporator_3byte_1 (
    .NUM1(bit_extender_1_out), .NUM2(24'h1), .EQUAL(comporator_3byte_1_equal));  // open: NUM1_GREATER
  not not_1 (not_1_out[0], comporator_3byte_1_equal);
  comporator_3byte comporator_3byte_2 (.NUM1(bit_extender_2_out), .NUM2(24'h12));  // open: NUM1_GREATER, EQUAL
  parsing parsing_1 (
    .NUM_16bit(transistor_1_out), .MANT_10bit(parsing_1_mant_10bit), .EXP_5bit(parsing_1_exp_5bit),
    .sign(parsing_1_sign[15]));
  not not_2 (not_2_out, not_1_out[0]);
  normalization_mant normalization_mant_1 (
    .exp(parsing_1_exp_5bit), .mant_10bit(parsing_1_mant_10bit),
    .res_exp_5bit(normalization_mant_1_res_exp_5bit), .mant_24bit(normalization_mant_1_mant_24bit));
  is_pos_inf is_pos_inf_1 (
    .sign(parsing_1_sign[15]), .exp(parsing_1_exp_5bit), .mant(parsing_1_mant_10bit), .res(is_pos_inf_1_res));
  is_neg_zero is_neg_zero_1 (
    .sign(parsing_1_sign[15]), .exp(parsing_1_exp_5bit), .mant(parsing_1_mant_10bit), .res(is_neg_zero_1_res));
  it_is_NaN it_is_nan_1 (.exp(parsing_1_exp_5bit), .mant(parsing_1_mant_10bit), .res(it_is_nan_1_res));
  is_neg_num is_neg_num_1 (
    .sign(parsing_1_sign[15]), .exp(parsing_1_exp_5bit), .mant(parsing_1_mant_10bit), .res(is_neg_num_1_res));
  assign bit_extender_3_out = {{19{normalization_mant_1_res_exp_5bit[4]}}, normalization_mant_1_res_exp_5bit};  // Bit_Extender bit_extender_3
  or or_1 (or_1_out, is_pos_inf_1_res, is_neg_zero_1_res, it_is_nan_1_res, is_neg_num_1_res);
  if_24bit if_24bit_1 (
    .Value_1(normalization_mant_1_mant_24bit), .expression(not_2_out), .Value_2(memory_3byte_3_out_num),
    .result(if_24bit_1_result));
  quite_Nan quite_nan_1 (.QNAN(quite_nan_1_qnan));
  not not_3 (not_3_out, not_1_out[0]);
  or or_2 (or_2_out, it_is_nan_1_res, is_neg_num_1_res);
  not not_4 (not_4_out, CLK);
  if_16bit if_16bit_1 (
    .Value_1(quite_nan_1_qnan), .expression(is_neg_num_1_res),
    .Value_2({parsing_1_sign[15], parsing_1_exp_5bit, parsing_1_mant_10bit}));  // open: result
  // Probe on memory_3byte_1_out_num
  memory_3byte memory_3byte_1 (
    .num_24bit(bit_extender_3_out), .C(not_3_out), .ENABLE(ENABLE), .OUT_NUM(memory_3byte_1_out_num));
  memory_3byte memory_3byte_2 (
    .num_24bit(if_24bit_1_result), .C(CLK), .ENABLE(ENABLE), .OUT_NUM(memory_3byte_2_out_num));
  memory_3byte memory_3byte_3 (
    .num_24bit(left_shift_2_res_24bit), .C(not_4_out), .ENABLE(ENABLE), .OUT_NUM(memory_3byte_3_out_num));
  // Probe on memory_3byte_2_out_num
  RSC_trigger rsc_trigger_1 (.R(1'b0), .C(CLK), .S(or_2_out), .enable(ENABLE), .Q(IS_NAN));  // open: not_Q
  RSC_trigger rsc_trigger_2 (.R(1'b0), .C(CLK), .S(is_pos_inf_1_res), .enable(ENABLE), .Q(IS_PINF));  // open: not_Q
  or or_3 (or_3_out, or_1_out, 1'b0);
  // Probe on new_exp_1_new_exp_24bit
  new_exp new_exp_1 (.exp_24bit(memory_3byte_1_out_num), .new_exp_24bit(new_exp_1_new_exp_24bit));
  left_shift left_shift_1 (.num_24bit(memory_3byte_2_out_num), .res_24bit(left_shift_1_res_24bit));
  RSC_trigger rsc_trigger_3 (.R(1'b0), .C(CLK), .S(or_3_out), .enable(ENABLE), .Q(RESULT));  // open: not_Q
  not not_5 (not_5_out, RESULT);
  and and_1 (and_1_out, not_5_out, ENABLE);
  left_shift left_shift_2 (.num_24bit(left_shift_1_res_24bit), .res_24bit(left_shift_2_res_24bit));
  not not_6 (not_6_out, CLK);
  not not_7 (not_7_out, CLK);
  memory_3byte res_read (
    .num_24bit(res_write_out_num), .C(CLK), .ENABLE(and_1_out), .OUT_NUM({res_read_out_num, mant_res}));
  memory_3byte res_write (
    .num_24bit(if_24bit_2_result), .C(not_6_out), .ENABLE(and_1_out), .OUT_NUM(res_write_out_num));
  memory_3byte remainder_read (
    .num_24bit(remainder_write_out_num), .C(CLK), .ENABLE(and_1_out), .OUT_NUM(remainder_read_out_num));
  memory_3byte remainder_write (
    .num_24bit(if_24bit_3_result), .C(not_7_out), .ENABLE(and_1_out), .OUT_NUM(remainder_write_out_num));
  // Probe on remainder_write_out_num
  // Probe on mant_res
  left_shift left_shift_3 (.num_24bit({res_read_out_num, mant_res}), .res_24bit(left_shift_3_res_24bit));
  left_shift left_shift_4 (.num_24bit(remainder_read_out_num), .res_24bit(left_shift_4_res_24bit));
  assign bit_extender_4_out = {{22{1'b0}}, memory_3byte_2_out_num[11:10]};  // Bit_Extender bit_extender_4
  left_shift left_shift_5 (.num_24bit(left_shift_4_res_24bit), .res_24bit(left_shift_5_res_24bit));
  left_shift left_shift_6 (.num_24bit(left_shift_3_res_24bit), .res_24bit(left_shift_6_res_24bit));
  summator_3byte summator_3byte_1 (
    .X_24bit(left_shift_3_res_24bit), .Y_24bit(24'h1), .RES_24bit(summator_3byte_1_res_24bit));
  summator_3byte summator_3byte_2 (
    .X_24bit(bit_extender_4_out), .Y_24bit(left_shift_5_res_24bit), .RES_24bit(summator_3byte_2_res_24bit));
  summator_3byte summator_3byte_3 (
    .X_24bit(left_shift_6_res_24bit), .Y_24bit(24'h1), .RES_24bit(summator_3byte_3_res_24bit));
  comporator_3byte comporator_3byte_3 (
    .NUM1(summator_3byte_2_res_24bit), .NUM2(summator_3byte_3_res_24bit),
    .NUM1_GREATER(comporator_3byte_3_num1_greater), .EQUAL(comporator_3byte_3_equal));
  or or_4 (or_4_out, comporator_3byte_3_num1_greater, comporator_3byte_3_equal);
  substractor_3byte substractor_3byte_1 (
    .X_24bit(summator_3byte_2_res_24bit), .Y_24bit(summator_3byte_3_res_24bit),
    .RES_24bit(substractor_3byte_1_res_24bit));
  if_24bit if_24bit_2 (
    .Value_1(summator_3byte_1_res_24bit), .expression(or_4_out), .Value_2(left_shift_3_res_24bit),
    .result(if_24bit_2_result));
  if_24bit if_24bit_3 (
    .Value_1(substractor_3byte_1_res_24bit), .expression(or_4_out), .Value_2(summator_3byte_2_res_24bit),
    .result(if_24bit_3_result));
  // Pins of 1 and 16 bits meet at not_1_out

  assign IO_DATA_OUT = IO_DATA_IN;
  assign IS_NINF = 1'b0;

  // Other names for the same wires on the sheet: enble = ENABLE; synch = CLK
endmodule

module full_substracter (
  input  X,
  input  Y,
  input  B_in,
  output D,
  output B_out
);

  wire and_1_out, and_2_out, not_1_out, not_2_out, xor_1_out;

  xor xor_1 (xor_1_out, X, Y);
  not not_1 (not_1_out, X);
  and and_1 (and_1_out, not_1_out, Y);
  not not_2 (not_2_out, xor_1_out);
  xor xor_2 (D, xor_1_out, B_in);
  and and_2 (and_2_out, B_in, not_2_out);
  or or_1 (B_out, and_2_out, and_1_out);
endmodule

module substractor_byte (
  input  [7:0] X_8bit,
  input  [7:0] Y_8bit,
  input  BORROW_IN,
  output [7:0] res_8bit,
  output BORROW_OUT
);

  wire full_substracter_1_b_out, full_substracter_2_b_out, full_substracter_3_b_out,
       full_substracter_4_b_out, full_substracter_5_b_out, full_substracter_6_b_out, full_substracter_7_b_out;

  full_substracter full_substracter_1 (
    .X(X_8bit[0]), .Y(Y_8bit[0]), .B_in(BORROW_IN), .D(res_8bit[0]), .B_out(full_substracter_1_b_out));
  full_substracter full_substracter_2 (
    .X(X_8bit[1]), .Y(Y_8bit[1]), .B_in(full_substracter_1_b_out), .D(res_8bit[1]),
    .B_out(full_substracter_2_b_out));
  full_substracter full_substracter_3 (
    .X(X_8bit[2]), .Y(Y_8bit[2]), .B_in(full_substracter_2_b_out), .D(res_8bit[2]),
    .B_out(full_substracter_3_b_out));
  full_substracter full_substracter_4 (
    .X(X_8bit[3]), .Y(Y_8bit[3]), .B_in(full_substracter_3_b_out), .D(res_8bit[3]),
    .B_out(full_substracter_4_b_out));
  full_substracter full_substracter_5 (
    .X(X_8bit[4]), .Y(Y_8bit[4]), .B_in(full_substracter_4_b_out), .D(res_8bit[4]),
    .B_out(full_substracter_5_b_out));
  full_substracter full_substracter_6 (
    .X(X_8bit[5]), .Y(Y_8bit[5]), .B_in(full_substracter_5_b_out), .D(res_8bit[5]),
    .B_out(full_substracter_6_b_out));
  full_substracter full_substracter_7 (
    .X(X_8bit[6]), .Y(Y_8bit[6]), .B_in(full_substracter_6_b_out), .D(res_8bit[6]),
    .B_out(full_substracter_7_b_out));
  full_substracter full_substracter_8 (
    .X(X_8bit[7]), .Y(Y_8bit[7]), .B_in(full_substracter_7_b_out), .D(res_8bit[7]), .B_out(BORROW_OUT));
endmodule

module substractor_3byte (
  input  [23:0] X_24bit,
  input  [23:0] Y_24bit,
  output [23:0] RES_24bit
);

  wire substractor_byte_1_borrow_out, substractor_byte_2_borrow_out;

  substractor_byte substractor_byte_1 (
    .X_8bit(X_24bit[7:0]), .Y_8bit(Y_24bit[7:0]), .BORROW_IN(1'b0), .res_8bit(RES_24bit[7:0]),
    .BORROW_OUT(substractor_byte_1_borrow_out));
  substractor_byte substractor_byte_2 (
    .X_8bit(X_24bit[15:8]), .Y_8bit(Y_24bit[15:8]), .BORROW_IN(substractor_byte_1_borrow_out),
    .res_8bit(RES_24bit[15:8]), .BORROW_OUT(substractor_byte_2_borrow_out));
  substractor_byte substractor_byte_3 (
    .X_8bit(X_24bit[23:16]), .Y_8bit(Y_24bit[23:16]), .BORROW_IN(substractor_byte_2_borrow_out),
    .res_8bit(RES_24bit[23:16]));  // open: BORROW_OUT
endmodule

module comporator_bit (
  input  Bit_1,
  input  Bit_2,
  input  prev_gt,
  input  prev_eq,
  output greater,
  output equal
);

  wire and_1_out, not_1_out, xnor_1_out;

  not not_1 (not_1_out, Bit_2);
  xnor xnor_1 (xnor_1_out, Bit_1, Bit_2);
  and and_1 (and_1_out, Bit_1, not_1_out, prev_eq);
  or or_1 (greater, and_1_out, prev_gt);
  and and_2 (equal, xnor_1_out, prev_eq);
endmodule

module comporator_byte (
  input  [7:0] X_8bit,
  input  [7:0] Y_8bit,
  input  PREV_X_GREATER,
  input  PREV_EQUAL,
  output X_GREATER,
  output EQUAL
);

  wire comporator_bit_2_equal, comporator_bit_2_greater, comporator_bit_3_equal, comporator_bit_3_greater,
       comporator_bit_4_equal, comporator_bit_4_greater, comporator_bit_5_equal, comporator_bit_5_greater,
       comporator_bit_6_equal, comporator_bit_6_greater, comporator_bit_7_equal, comporator_bit_7_greater,
       comporator_bit_8_equal, comporator_bit_8_greater;

  comporator_bit comporator_bit_1 (
    .Bit_1(X_8bit[0]), .Bit_2(Y_8bit[0]), .prev_gt(comporator_bit_2_greater),
    .prev_eq(comporator_bit_2_equal), .greater(X_GREATER), .equal(EQUAL));
  comporator_bit comporator_bit_2 (
    .Bit_1(X_8bit[1]), .Bit_2(Y_8bit[1]), .prev_gt(comporator_bit_3_greater),
    .prev_eq(comporator_bit_3_equal), .greater(comporator_bit_2_greater), .equal(comporator_bit_2_equal));
  comporator_bit comporator_bit_3 (
    .Bit_1(X_8bit[2]), .Bit_2(Y_8bit[2]), .prev_gt(comporator_bit_4_greater),
    .prev_eq(comporator_bit_4_equal), .greater(comporator_bit_3_greater), .equal(comporator_bit_3_equal));
  comporator_bit comporator_bit_4 (
    .Bit_1(X_8bit[3]), .Bit_2(Y_8bit[3]), .prev_gt(comporator_bit_5_greater),
    .prev_eq(comporator_bit_5_equal), .greater(comporator_bit_4_greater), .equal(comporator_bit_4_equal));
  comporator_bit comporator_bit_5 (
    .Bit_1(X_8bit[4]), .Bit_2(Y_8bit[4]), .prev_gt(comporator_bit_6_greater),
    .prev_eq(comporator_bit_6_equal), .greater(comporator_bit_5_greater), .equal(comporator_bit_5_equal));
  comporator_bit comporator_bit_6 (
    .Bit_1(X_8bit[5]), .Bit_2(Y_8bit[5]), .prev_gt(comporator_bit_7_greater),
    .prev_eq(comporator_bit_7_equal), .greater(comporator_bit_6_greater), .equal(comporator_bit_6_equal));
  comporator_bit comporator_bit_7 (
    .Bit_1(X_8bit[6]), .Bit_2(Y_8bit[6]), .prev_gt(comporator_bit_8_greater),
    .prev_eq(comporator_bit_8_equal), .greater(comporator_bit_7_greater), .equal(comporator_bit_7_equal));
  comporator_bit comporator_bit_8 (
    .Bit_1(X_8bit[7]), .Bit_2(Y_8bit[7]), .prev_gt(PREV_X_GREATER), .prev_eq(PREV_EQUAL),
    .greater(comporator_bit_8_greater), .equal(comporator_bit_8_equal));
endmodule

module comporator_3byte (
  input  [23:0] NUM1,
  input  [23:0] NUM2,
  output NUM1_GREATER,
  output EQUAL
);

  wire comporator_byte_2_equal, comporator_byte_2_x_greater, comporator_byte_3_equal,
       comporator_byte_3_x_greater;

  comporator_byte comporator_byte_1 (
    .X_8bit(NUM1[7:0]), .Y_8bit(NUM2[7:0]), .PREV_X_GREATER(comporator_byte_2_x_greater),
    .PREV_EQUAL(comporator_byte_2_equal), .X_GREATER(NUM1_GREATER), .EQUAL(EQUAL));
  comporator_byte comporator_byte_2 (
    .X_8bit(NUM1[15:8]), .Y_8bit(NUM2[15:8]), .PREV_X_GREATER(comporator_byte_3_x_greater),
    .PREV_EQUAL(comporator_byte_3_equal), .X_GREATER(comporator_byte_2_x_greater),
    .EQUAL(comporator_byte_2_equal));
  comporator_byte comporator_byte_3 (
    .X_8bit(NUM1[23:16]), .Y_8bit(NUM2[23:16]), .PREV_X_GREATER(1'b0), .PREV_EQUAL(1'b1),
    .X_GREATER(comporator_byte_3_x_greater), .EQUAL(comporator_byte_3_equal));
endmodule

module RS_trigger (
  input  R,
  input  S,
  input  enable,
  output Q,
  output not_Q
);

  wire nor_2_out, not_1_out, or_1_out, por_1_out;

  not not_1 (not_1_out, enable);
  POR por_1 (.out(por_1_out));
  nor nor_1 (Q, R, not_Q);
  nor nor_2 (nor_2_out, Q, S);
  or or_1 (or_1_out, not_1_out, por_1_out);
  or or_2 (not_Q, nor_2_out, or_1_out);
endmodule

module RSC_trigger (
  input  R,
  input  C,
  input  S,
  input  enable,
  output Q,
  output not_Q
);

  wire and_1_out, and_2_out;

  and and_1 (and_1_out, R, C);
  and and_2 (and_2_out, C, S);
  RS_trigger rs_trigger_1 (.R(and_1_out), .S(and_2_out), .enable(enable), .Q(Q), .not_Q(not_Q));
endmodule

module D_trigger (
  input  C,
  input  D,
  input  enable,
  output Q,
  output not_Q
);

  wire not_1_out;

  not not_1 (not_1_out, D);
  RSC_trigger rsc_trigger_1 (.R(not_1_out), .C(C), .S(D), .enable(enable), .Q(Q), .not_Q(not_Q));
endmodule

module jk_trigger (
  input  K,
  input  C,
  input  J,
  input  enable,
  output Q,
  output not_Q
);

  wire and_1_out, and_2_out, not_1_out, rsc_trigger_1_not_q, rsc_trigger_1_q;

  and and_1 (and_1_out, Q, K);
  and and_2 (and_2_out, J, not_Q);
  not not_1 (not_1_out, C);
  RSC_trigger rsc_trigger_1 (
    .R(and_1_out), .C(C), .S(and_2_out), .enable(enable), .Q(rsc_trigger_1_q), .not_Q(rsc_trigger_1_not_q));
  RSC_trigger rsc_trigger_2 (
    .R(rsc_trigger_1_not_q), .C(not_1_out), .S(rsc_trigger_1_q), .enable(enable), .Q(Q), .not_Q(not_Q));
endmodule

module summator (
  input  [11:0] num1_12bit,
  input  [11:0] num2_12bit,
  output [11:0] res_12bit
);

  wire summator_bit_1_carry_out, summator_bit_2_carry_out, summator_bit_3_carry_out,
       summator_bit_4_carry_out, summator_bit_5_carry_out, summator_bit_6_carry_out,
       summator_bit_7_carry_out, summator_bit_8_carry_out, summator_bit_9_carry_out,
       summator_bit_10_carry_out, summator_bit_11_carry_out;

  summator_bit summator_bit_1 (
    .carry_in(1'b0), .bit_1(num1_12bit[0]), .bit_2(num2_12bit[0]), .res(res_12bit[0]),
    .carry_out(summator_bit_1_carry_out));
  summator_bit summator_bit_2 (
    .carry_in(summator_bit_1_carry_out), .bit_1(num1_12bit[1]), .bit_2(num2_12bit[1]), .res(res_12bit[1]),
    .carry_out(summator_bit_2_carry_out));
  summator_bit summator_bit_3 (
    .carry_in(summator_bit_2_carry_out), .bit_1(num1_12bit[2]), .bit_2(num2_12bit[2]), .res(res_12bit[2]),
    .carry_out(summator_bit_3_carry_out));
  summator_bit summator_bit_4 (
    .carry_in(summator_bit_3_carry_out), .bit_1(num1_12bit[3]), .bit_2(num2_12bit[3]), .res(res_12bit[3]),
    .carry_out(summator_bit_4_carry_out));
  summator_bit summator_bit_5 (
    .carry_in(summator_bit_4_carry_out), .bit_1(num1_12bit[4]), .bit_2(num2_12bit[4]), .res(res_12bit[4]),
    .carry_out(summator_bit_5_carry_out));
  summator_bit summator_bit_6 (
    .carry_in(summator_bit_5_carry_out), .bit_1(num1_12bit[5]), .bit_2(num2_12bit[5]), .res(res_12bit[5]),
    .carry_out(summator_bit_6_carry_out));
  summator_bit summator_bit_7 (
    .carry_in(summator_bit_6_carry_out), .bit_1(num1_12bit[6]), .bit_2(num2_12bit[6]), .res(res_12bit[6]),
    .carry_out(summator_bit_7_carry_out));
  summator_bit summator_bit_8 (
    .carry_in(summator_bit_7_carry_out), .bit_1(num1_12bit[7]), .bit_2(num2_12bit[7]), .res(res_12bit[7]),
    .carry_out(summator_bit_8_carry_out));
  summator_bit summator_bit_9 (
    .carry_in(summator_bit_8_carry_out), .bit_1(num1_12bit[8]), .bit_2(num2_12bit[8]), .res(res_12bit[8]),
    .carry_out(summator_bit_9_carry_out));
  summator_bit summator_bit_10 (
    .carry_in(summator_bit_9_carry_out), .bit_1(num1_12bit[9]), .bit_2(num2_12bit[9]), .res(res_12bit[9]),
    .carry_out(summator_bit_10_carry_out));
  summator_bit summator_bit_11 (
    .carry_in(summator_bit_10_carry_out), .bit_1(num1_12bit[10]), .bit_2(num2_12bit[10]),
    .res(res_12bit[10]), .carry_out(summator_bit_11_carry_out));
  summator_bit summator_bit_12 (
    .carry_in(summator_bit_11_carry_out), .bit_1(num1_12bit[11]), .bit_2(num2_12bit[11]), .res(res_12bit[11]));  // open: carry_out
endmodule

module summator_bit (
  input  carry_in,
  input  bit_1,
  input  bit_2,
  output res,
  output carry_out
);

  wire and_1_out, and_2_out, xor_1_out;

  xor xor_1 (xor_1_out, bit_1, bit_2);
  and and_1 (and_1_out, bit_1, bit_2);
  xor xor_2 (res, carry_in, xor_1_out);
  and and_2 (and_2_out, carry_in, xor_1_out);
  or or_1 (carry_out, and_2_out, and_1_out);
endmodule

module summator_byte (
  input  CARRY_IN,
  input  [7:0] X_8bit,
  input  [7:0] Y_8bit,
  output [7:0] RES_8bit,
  output CARRY_OUT
);

  wire summator_bit_1_carry_out, summator_bit_2_carry_out, summator_bit_3_carry_out,
       summator_bit_4_carry_out, summator_bit_5_carry_out, summator_bit_6_carry_out, summator_bit_7_carry_out;

  summator_bit summator_bit_1 (
    .carry_in(CARRY_IN), .bit_1(X_8bit[0]), .bit_2(Y_8bit[0]), .res(RES_8bit[0]),
    .carry_out(summator_bit_1_carry_out));
  summator_bit summator_bit_2 (
    .carry_in(summator_bit_1_carry_out), .bit_1(X_8bit[1]), .bit_2(Y_8bit[1]), .res(RES_8bit[1]),
    .carry_out(summator_bit_2_carry_out));
  summator_bit summator_bit_3 (
    .carry_in(summator_bit_2_carry_out), .bit_1(X_8bit[2]), .bit_2(Y_8bit[2]), .res(RES_8bit[2]),
    .carry_out(summator_bit_3_carry_out));
  summator_bit summator_bit_4 (
    .carry_in(summator_bit_3_carry_out), .bit_1(X_8bit[3]), .bit_2(Y_8bit[3]), .res(RES_8bit[3]),
    .carry_out(summator_bit_4_carry_out));
  summator_bit summator_bit_5 (
    .carry_in(summator_bit_4_carry_out), .bit_1(X_8bit[4]), .bit_2(Y_8bit[4]), .res(RES_8bit[4]),
    .carry_out(summator_bit_5_carry_out));
  summator_bit summator_bit_6 (
    .carry_in(summator_bit_5_carry_out), .bit_1(X_8bit[5]), .bit_2(Y_8bit[5]), .res(RES_8bit[5]),
    .carry_out(summator_bit_6_carry_out));
  summator_bit summator_bit_7 (
    .carry_in(summator_bit_6_carry_out), .bit_1(X_8bit[6]), .bit_2(Y_8bit[6]), .res(RES_8bit[6]),
    .carry_out(summator_bit_7_carry_out));
  summator_bit summator_bit_8 (
    .carry_in(summator_bit_7_carry_out), .bit_1(X_8bit[7]), .bit_2(Y_8bit[7]), .res(RES_8bit[7]),
    .carry_out(CARRY_OUT));
endmodule

module summator_3byte (
  input  [23:0] X_24bit,
  input  [23:0] Y_24bit,
  output [23:0] RES_24bit
);

  wire summator_byte_1_carry_out, summator_byte_2_carry_out;

  summator_byte summator_byte_1 (
    .CARRY_IN(1'b0), .X_8bit(X_24bit[7:0]), .Y_8bit(Y_24bit[7:0]), .RES_8bit(RES_24bit[7:0]),
    .CARRY_OUT(summator_byte_1_carry_out));
  summator_byte summator_byte_2 (
    .CARRY_IN(summator_byte_1_carry_out), .X_8bit(X_24bit[15:8]), .Y_8bit(Y_24bit[15:8]),
    .RES_8bit(RES_24bit[15:8]), .CARRY_OUT(summator_byte_2_carry_out));
  summator_byte summator_byte_3 (
    .CARRY_IN(summator_byte_2_carry_out), .X_8bit(X_24bit[23:16]), .Y_8bit(Y_24bit[23:16]),
    .RES_8bit(RES_24bit[23:16]));  // open: CARRY_OUT
endmodule

module parsing (
  input  [15:0] NUM_16bit,
  output [9:0] MANT_10bit,
  output [4:0] EXP_5bit,
  output sign
);


  assign EXP_5bit = NUM_16bit[14:10];
  assign MANT_10bit = NUM_16bit[9:0];
  assign sign = NUM_16bit[15];
endmodule

module is_pos_inf (
  input  sign,
  input  [4:0] exp,
  input  [9:0] mant,
  output res
);

  wire comporator_3byte_1_equal, comporator_3byte_2_equal, not_1_out;
  wire [23:0] bit_extender_1_out, bit_extender_2_out;

  assign bit_extender_1_out = {{19{1'b0}}, exp};  // Bit_Extender bit_extender_1
  assign bit_extender_2_out = {{14{1'b0}}, mant};  // Bit_Extender bit_extender_2
  not not_1 (not_1_out, sign);
  comporator_3byte comporator_3byte_1 (
    .NUM1(bit_extender_1_out), .NUM2(24'h1f), .EQUAL(comporator_3byte_1_equal));  // open: NUM1_GREATER
  comporator_3byte comporator_3byte_2 (
    .NUM1(bit_extender_2_out), .NUM2({24{1'b0}}), .EQUAL(comporator_3byte_2_equal));  // open: NUM1_GREATER
  and and_1 (res, not_1_out, comporator_3byte_1_equal, comporator_3byte_2_equal);
endmodule

module is_pos_zero (
  input  sign,
  input  [4:0] exp,
  input  [9:0] mant,
  output res
);

  wire comporator_3byte_1_equal, comporator_3byte_2_equal, not_1_out;
  wire [23:0] bit_extender_1_out, bit_extender_2_out;

  not not_1 (not_1_out, sign);
  assign bit_extender_1_out = {{19{1'b0}}, exp};  // Bit_Extender bit_extender_1
  assign bit_extender_2_out = {{14{1'b0}}, mant};  // Bit_Extender bit_extender_2
  comporator_3byte comporator_3byte_1 (
    .NUM1(bit_extender_1_out), .NUM2({24{1'b0}}), .EQUAL(comporator_3byte_1_equal));  // open: NUM1_GREATER
  comporator_3byte comporator_3byte_2 (
    .NUM1(bit_extender_2_out), .NUM2({24{1'b0}}), .EQUAL(comporator_3byte_2_equal));  // open: NUM1_GREATER
  and and_1 (res, not_1_out, comporator_3byte_1_equal, comporator_3byte_2_equal);
endmodule

module is_neg_zero (
  input  sign,
  input  [4:0] exp,
  input  [9:0] mant,
  output res
);

  wire comporator_3byte_1_equal, comporator_3byte_2_equal;
  wire [23:0] bit_extender_1_out, bit_extender_2_out;

  assign bit_extender_1_out = {{19{1'b0}}, exp};  // Bit_Extender bit_extender_1
  assign bit_extender_2_out = {{14{1'b0}}, mant};  // Bit_Extender bit_extender_2
  comporator_3byte comporator_3byte_1 (
    .NUM1(bit_extender_1_out), .NUM2({24{1'b0}}), .EQUAL(comporator_3byte_1_equal));  // open: NUM1_GREATER
  comporator_3byte comporator_3byte_2 (
    .NUM1(bit_extender_2_out), .NUM2({24{1'b0}}), .EQUAL(comporator_3byte_2_equal));  // open: NUM1_GREATER
  and and_1 (res, sign, comporator_3byte_1_equal, comporator_3byte_2_equal);
endmodule

module quite_Nan (
  output [15:0] QNAN
);


  assign QNAN = 16'hfe00;
endmodule

module it_is_NaN (
  input  [4:0] exp,
  input  [9:0] mant,
  output res
);

  wire comporator_3byte_1_equal, comporator_3byte_2_equal, not_1_out;
  wire [23:0] bit_extender_1_out, bit_extender_2_out;

  assign bit_extender_1_out = {{19{exp[4]}}, exp};  // Bit_Extender bit_extender_1
  assign bit_extender_2_out = {{14{mant[9]}}, mant};  // Bit_Extender bit_extender_2
  comporator_3byte comporator_3byte_1 (
    .NUM1(bit_extender_1_out), .NUM2(24'h1f), .EQUAL(comporator_3byte_1_equal));  // open: NUM1_GREATER
  comporator_3byte comporator_3byte_2 (
    .NUM1(bit_extender_2_out), .NUM2({24{1'b0}}), .EQUAL(comporator_3byte_2_equal));  // open: NUM1_GREATER
  not not_1 (not_1_out, comporator_3byte_2_equal);
  and and_1 (res, comporator_3byte_1_equal, not_1_out);
endmodule

module is_neg_num (
  input  sign,
  input  [4:0] exp,
  input  [9:0] mant,
  output res
);

  wire is_neg_zero_1_res, it_is_nan_1_res, not_1_out, not_2_out;

  is_neg_zero is_neg_zero_1 (.sign(sign), .exp(exp), .mant(mant), .res(is_neg_zero_1_res));
  it_is_NaN it_is_nan_1 (.exp(exp), .mant(mant), .res(it_is_nan_1_res));
  not not_1 (not_1_out, is_neg_zero_1_res);
  not not_2 (not_2_out, it_is_nan_1_res);
  and and_1 (res, sign, not_1_out, not_2_out);
endmodule

module if_12bit (
  input  [11:0] Value_1,
  input  expression,
  input  [11:0] Value_2,
  output [11:0] result
);

  wire not_1_out;

  not not_1 (not_1_out, expression);
  Transistor #(.\type ("n"), .width(12)) transistor_1 (.in(Value_1), .out(result), .gate(expression));
  Transistor #(.\type ("n"), .width(12)) transistor_2 (.in(Value_2), .out(result), .gate(not_1_out));
  Pull_Resistor #(.pull(1)) pull_resistor_1 (.node(result));
endmodule

module if_16bit (
  input  [15:0] Value_1,
  input  expression,
  input  [15:0] Value_2,
  output [15:0] result
);

  wire not_1_out;

  not not_1 (not_1_out, expression);
  Transistor #(.\type ("n"), .width(16)) transistor_1 (.in(Value_1), .out(result), .gate(expression));
  Transistor #(.\type ("n"), .width(16)) transistor_2 (.in(Value_2), .out(result), .gate(not_1_out));
  Pull_Resistor #(.pull(1)) pull_resistor_1 (.node(result));
endmodule

module if_24bit (
  input  [23:0] Value_1,
  input  expression,
  input  [23:0] Value_2,
  output [23:0] result
);

  wire not_1_out;

  Transistor #(.\type ("n"), .width(24)) transistor_1 (.in(Value_1), .out(result), .gate(expression));
  not not_1 (not_1_out, expression);
  Transistor #(.\type ("n"), .width(24)) transistor_2 (.in(Value_2), .out(result), .gate(not_1_out));
  Pull_Resistor #(.pull(1)) pull_resistor_1 (.node(result));
endmodule

module normalization_mant (
  input  [4:0] exp,
  input  [9:0] mant_10bit,
  output [4:0] res_exp_5bit,
  output [23:0] mant_24bit
);

  wire [18:0] if_24bit_2_result;
  wire [23:0] bit_extender_1_out, bit_extender_2_out, bit_extender_3_out, left_shift_1_res_24bit,
       substractor_3byte_1_res_24bit;

  assign bit_extender_1_out = {{12{1'b0}}, {2'b01, mant_10bit}};  // Bit_Extender bit_extender_1
  assign bit_extender_2_out = {{19{1'b0}}, exp};  // Bit_Extender bit_extender_2
  substractor_3byte substractor_3byte_1 (
    .X_24bit(bit_extender_2_out), .Y_24bit(24'h1), .RES_24bit(substractor_3byte_1_res_24bit));
  left_shift left_shift_1 (.num_24bit(bit_extender_1_out), .res_24bit(left_shift_1_res_24bit));
  assign bit_extender_3_out = {{19{exp[4]}}, exp};  // Bit_Extender bit_extender_3
  if_24bit if_24bit_1 (
    .Value_1(bit_extender_1_out), .expression(exp[0]), .Value_2(left_shift_1_res_24bit), .result(mant_24bit));
  if_24bit if_24bit_2 (
    .Value_1(bit_extender_3_out), .expression(exp[0]), .Value_2(substractor_3byte_1_res_24bit),
    .result({if_24bit_2_result, res_exp_5bit}));
endmodule

module new_exp (
  input  [23:0] exp_24bit,
  output [23:0] new_exp_24bit
);

  wire comporator_3byte_1_equal, comporator_3byte_1_num1_greater, or_1_out;
  wire [23:0] if_24bit_1_result, right_shift_1_res_24bit, right_shift_2_res_24bit,
       substractor_3byte_1_res_24bit, substractor_3byte_2_res_24bit, substractor_3byte_3_res_24bit,
       substractor_3byte_4_res_24bit, summator_3byte_1_res_24bit;

  substractor_3byte substractor_3byte_1 (
    .X_24bit(exp_24bit), .Y_24bit(24'hf), .RES_24bit(substractor_3byte_1_res_24bit));
  substractor_3byte substractor_3byte_2 (
    .X_24bit(24'hf), .Y_24bit(exp_24bit), .RES_24bit(substractor_3byte_2_res_24bit));
  comporator_3byte comporator_3byte_1 (
    .NUM1(exp_24bit), .NUM2(24'hf), .NUM1_GREATER(comporator_3byte_1_num1_greater),
    .EQUAL(comporator_3byte_1_equal));
  right_shift right_shift_1 (.num_24bit(substractor_3byte_2_res_24bit), .res_24bit(right_shift_1_res_24bit));
  right_shift right_shift_2 (.num_24bit(substractor_3byte_1_res_24bit), .res_24bit(right_shift_2_res_24bit));
  or or_1 (or_1_out, comporator_3byte_1_num1_greater, comporator_3byte_1_equal);
  summator_3byte summator_3byte_1 (
    .X_24bit(right_shift_2_res_24bit), .Y_24bit(24'hf), .RES_24bit(summator_3byte_1_res_24bit));
  substractor_3byte substractor_3byte_3 (
    .X_24bit(24'hf), .Y_24bit(right_shift_1_res_24bit), .RES_24bit(substractor_3byte_3_res_24bit));
  if_24bit if_24bit_1 (
    .Value_1(summator_3byte_1_res_24bit), .expression(or_1_out), .Value_2(substractor_3byte_3_res_24bit),
    .result(if_24bit_1_result));
  substractor_3byte substractor_3byte_4 (
    .X_24bit(if_24bit_1_result), .Y_24bit(24'h1), .RES_24bit(substractor_3byte_4_res_24bit));
  if_24bit if_24bit_2 (
    .Value_1(if_24bit_1_result), .expression(exp_24bit[0]), .Value_2(substractor_3byte_4_res_24bit),
    .result(new_exp_24bit));

  // Other names for the same wires on the sheet: exp[23:0] = exp_24bit
endmodule

module counter (
  input  C,
  input  enable,
  output [15:0] value_16bit
);

  wire jk_trigger_1_not_q, jk_trigger_2_not_q, jk_trigger_3_not_q, not_1_out, not_2_out, not_3_out, not_4_out;
  wire [3:0] jk_trigger_1_q;

  not not_1 (not_1_out, C);
  jk_trigger jk_trigger_1 (
    .K(1'b1), .C(not_1_out), .J(1'b1), .enable(enable), .Q(jk_trigger_1_q[0]), .not_Q(jk_trigger_1_not_q));
  not not_2 (not_2_out, jk_trigger_1_not_q);
  jk_trigger jk_trigger_2 (
    .K(1'b1), .C(not_2_out), .J(1'b1), .enable(enable), .Q(jk_trigger_1_q[1]), .not_Q(jk_trigger_2_not_q));
  not not_3 (not_3_out, jk_trigger_2_not_q);
  jk_trigger jk_trigger_3 (
    .K(1'b1), .C(not_3_out), .J(1'b1), .enable(enable), .Q(jk_trigger_1_q[2]), .not_Q(jk_trigger_3_not_q));
  not not_4 (not_4_out, jk_trigger_3_not_q);
  jk_trigger jk_trigger_4 (.K(1'b1), .C(not_4_out), .J(1'b1), .enable(enable), .Q(jk_trigger_1_q[3]));  // open: not_Q
  assign value_16bit = {{12{1'b0}}, jk_trigger_1_q};  // Bit_Extender bit_extender_1
endmodule

module left_shift (
  input  [23:0] num_24bit,
  output [23:0] res_24bit
);


  assign res_24bit = {num_24bit[22:0], 1'b0};
endmodule

module right_shift (
  input  [23:0] num_24bit,
  output [23:0] res_24bit
);

  assign res_24bit = {{1{1'b0}}, num_24bit[23:1]};  // Bit_Extender bit_extender_1
endmodule

module denorm_to_norm (
  input  [23:0] exp_24bit,
  input  [23:0] mant_24bit,
  output [23:0] shift_exp,
  output [23:0] new_mant_24bit
);

  wire comporator_3byte_1_equal;
  wire [23:0] step_denorm_1_res_mant, step_denorm_1_res_shift, step_denorm_2_res_mant,
       step_denorm_2_res_shift, step_denorm_3_res_mant, step_denorm_3_res_shift, step_denorm_4_res_mant,
       step_denorm_4_res_shift, step_denorm_5_res_mant, step_denorm_5_res_shift, step_denorm_6_res_mant,
       step_denorm_6_res_shift, step_denorm_7_res_mant, step_denorm_7_res_shift, step_denorm_8_res_mant,
       step_denorm_8_res_shift, step_denorm_9_res_mant, step_denorm_9_res_shift, step_denorm_10_res_mant;

  step_denorm step_denorm_1 (
    .shift_exp_24bit({24{1'b0}}), .mant_24bit(mant_24bit), .res_shift(step_denorm_1_res_shift),
    .res_mant(step_denorm_1_res_mant));
  step_denorm step_denorm_2 (
    .shift_exp_24bit(step_denorm_9_res_shift), .mant_24bit(step_denorm_9_res_mant),
    .res_shift(step_denorm_2_res_shift), .res_mant(step_denorm_2_res_mant));
  step_denorm step_denorm_3 (
    .shift_exp_24bit(step_denorm_1_res_shift), .mant_24bit(step_denorm_1_res_mant),
    .res_shift(step_denorm_3_res_shift), .res_mant(step_denorm_3_res_mant));
  step_denorm step_denorm_4 (
    .shift_exp_24bit(step_denorm_2_res_shift), .mant_24bit(step_denorm_2_res_mant),
    .res_shift(step_denorm_4_res_shift), .res_mant(step_denorm_4_res_mant));
  comporator_3byte comporator_3byte_1 (
    .NUM1(exp_24bit), .NUM2({24{1'b0}}), .EQUAL(comporator_3byte_1_equal));  // open: NUM1_GREATER
  step_denorm step_denorm_5 (
    .shift_exp_24bit(step_denorm_3_res_shift), .mant_24bit(step_denorm_3_res_mant),
    .res_shift(step_denorm_5_res_shift), .res_mant(step_denorm_5_res_mant));
  step_denorm step_denorm_6 (
    .shift_exp_24bit(step_denorm_4_res_shift), .mant_24bit(step_denorm_4_res_mant),
    .res_shift(step_denorm_6_res_shift), .res_mant(step_denorm_6_res_mant));
  step_denorm step_denorm_7 (
    .shift_exp_24bit(step_denorm_5_res_shift), .mant_24bit(step_denorm_5_res_mant),
    .res_shift(step_denorm_7_res_shift), .res_mant(step_denorm_7_res_mant));
  step_denorm step_denorm_8 (
    .shift_exp_24bit(step_denorm_6_res_shift), .mant_24bit(step_denorm_6_res_mant),
    .res_shift(step_denorm_8_res_shift), .res_mant(step_denorm_8_res_mant));
  if_24bit if_24bit_1 (
    .Value_1(step_denorm_10_res_mant), .expression(comporator_3byte_1_equal), .Value_2(mant_24bit),
    .result(new_mant_24bit));
  step_denorm step_denorm_9 (
    .shift_exp_24bit(step_denorm_7_res_shift), .mant_24bit(step_denorm_7_res_mant),
    .res_shift(step_denorm_9_res_shift), .res_mant(step_denorm_9_res_mant));
  step_denorm step_denorm_10 (
    .shift_exp_24bit(step_denorm_8_res_shift), .mant_24bit(step_denorm_8_res_mant), .res_shift(shift_exp),
    .res_mant(step_denorm_10_res_mant));

  // Other names for the same wires on the sheet: mant[23:0] = mant_24bit
endmodule

module step_denorm (
  input  [23:0] shift_exp_24bit,
  input  [23:0] mant_24bit,
  output [23:0] res_shift,
  output [23:0] res_mant
);

  wire not_1_out;
  wire [23:0] left_shift_1_res_24bit, summator_3byte_1_res_24bit;

  summator_3byte summator_3byte_1 (.X_24bit(shift_exp_24bit), .Y_24bit(24'h1), .RES_24bit(summator_3byte_1_res_24bit));
  left_shift left_shift_1 (.num_24bit(mant_24bit), .res_24bit(left_shift_1_res_24bit));
  not not_1 (not_1_out, mant_24bit[10]);
  if_24bit if_24bit_1 (
    .Value_1(summator_3byte_1_res_24bit), .expression(not_1_out), .Value_2(shift_exp_24bit),
    .result(res_shift));
  if_24bit if_24bit_2 (
    .Value_1(left_shift_1_res_24bit), .expression(not_1_out), .Value_2(mant_24bit), .result(res_mant));
endmodule

module memory_byte (
  input  [7:0] number,
  input  c,
  input  enable,
  output [7:0] out_num
);

  D_trigger d_trigger_1 (.C(c), .D(number[0]), .enable(enable), .Q(out_num[0]));  // open: not_Q
  D_trigger d_trigger_2 (.C(c), .D(number[1]), .enable(enable), .Q(out_num[1]));  // open: not_Q
  D_trigger d_trigger_3 (.C(c), .D(number[2]), .enable(enable), .Q(out_num[2]));  // open: not_Q
  D_trigger d_trigger_4 (.C(c), .D(number[3]), .enable(enable), .Q(out_num[3]));  // open: not_Q
  D_trigger d_trigger_5 (.C(c), .D(number[4]), .enable(enable), .Q(out_num[4]));  // open: not_Q
  D_trigger d_trigger_6 (.C(c), .D(number[5]), .enable(enable), .Q(out_num[5]));  // open: not_Q
  D_trigger d_trigger_7 (.C(c), .D(number[6]), .enable(enable), .Q(out_num[6]));  // open: not_Q
  D_trigger d_trigger_8 (.C(c), .D(number[7]), .enable(enable), .Q(out_num[7]));  // open: not_Q
endmodule

module memory_3byte (
  input  [23:0] num_24bit,
  input  C,
  input  ENABLE,
  output [23:0] OUT_NUM
);

  memory_byte memory_byte_1 (.number(num_24bit[7:0]), .c(C), .enable(ENABLE), .out_num(OUT_NUM[7:0]));
  memory_byte memory_byte_2 (.number(num_24bit[15:8]), .c(C), .enable(ENABLE), .out_num(OUT_NUM[15:8]));
  memory_byte memory_byte_3 (.number(num_24bit[23:16]), .c(C), .enable(ENABLE), .out_num(OUT_NUM[23:16]));
endmodule
